// Logisim project I'm a MAZE.circ as structural Verilog: 7 circuits, main circuit main
module main (
  input  [2:0] in_1
);

  wire clk, controlled_buffer_1_out, keyboard_1_avail, start;
  wire [3:0] mux_1_out_27;
  wire [6:0] keyboard;
  wire [19:0] mux_1_out_4, mux_1_out_5, mux_1_out_6, mux_1_out_7, mux_1_out_8, mux_1_out_9, mux_1_out_10,
       mux_1_out_11, mux_1_out_12, mux_1_out_13, mux_1_out_14, mux_1_out_15, mux_1_out_18, mux_1_out_19,
       mux_1_out_20, mux_1_out_21, mux_1_out_22, mux_1_out_23, mux_1_out_24, mux_1_out_25, mux_1_out_26,
       mux_1_out_28, mux_1_out_29, mux_1_out_30, mux_1_out_31;

  Button button_1 (.out(start));
  Clock clock_1 (.out(clk));
  Hex_Digit_Display hex_digit_display_1 (.value(mux_1_out_27));  // open: dp
  DotMatrix #(.inputtype("row"), .matrixcols(20), .matrixrows(25)) dotmatrix_1 (
    .row0(mux_1_out_4), .row1(mux_1_out_5), .row2(mux_1_out_6), .row3(mux_1_out_7), .row4(mux_1_out_8),
    .row5(mux_1_out_9), .row6(mux_1_out_10), .row7(mux_1_out_11), .row8(mux_1_out_12), .row9(mux_1_out_13),
    .row10(mux_1_out_14), .row11(mux_1_out_15), .row12(mux_1_out_18), .row13(mux_1_out_19),
    .row14(mux_1_out_20), .row15(mux_1_out_21), .row16(mux_1_out_22), .row17(mux_1_out_23),
    .row18(mux_1_out_24), .row19(mux_1_out_25), .row20(mux_1_out_26), .row21(mux_1_out_28),
    .row22(mux_1_out_29), .row23(mux_1_out_30), .row24(mux_1_out_31));
  mux mux_1 (
    .keyboard(keyboard), .in_2(in_1), .in_1(start), .out_27(mux_1_out_27), .out_4(mux_1_out_4),
    .out_5(mux_1_out_5), .out_6(mux_1_out_6), .out_7(mux_1_out_7), .out_8(mux_1_out_8), .out_9(mux_1_out_9),
    .out_10(mux_1_out_10), .out_11(mux_1_out_11), .out_12(mux_1_out_12), .out_13(mux_1_out_13),
    .out_14(mux_1_out_14), .out_15(mux_1_out_15), .out_18(mux_1_out_18), .out_19(mux_1_out_19),
    .out_20(mux_1_out_20), .out_21(mux_1_out_21), .out_22(mux_1_out_22), .out_23(mux_1_out_23),
    .out_24(mux_1_out_24), .out_25(mux_1_out_25), .out_26(mux_1_out_26), .out_28(mux_1_out_28),
    .out_29(mux_1_out_29), .out_30(mux_1_out_30), .out_31(mux_1_out_31));  // open: out_16, out_17, out_32
  TTY tty_1 (.data(keyboard), .clk(clk));  // open: we, clr
  assign controlled_buffer_1_out = keyboard_1_avail ? clk : 1'bz;  // Controlled_Buffer controlled_buffer_1
  Keyboard keyboard_1 (.clk(controlled_buffer_1_out), .avail(keyboard_1_avail), .data(keyboard));  // open: re, clr

  // Other names for the same wires on the sheet: startstage[2:0] = in_1

  // Notes on the sheet:
  //   life
  //   Start
  //   Goal
  //   I'm a MAZE
  //   Gameplay :
  //   HOW-TO-WIN :
  //   สมาชิก
  //   น.ส.ณิชชารีย์ คัคนางค์จนันท์  6210612617
  //   น.ส.กชกร สุรินทร์  6210612674
  //   นายสิทธิโชค งามพิพัฒน์โชคชัย  6210612815
  //   เมื่อเราเข้า Goal ครบทั้งสามเสตจ จะปรากฎหน้า VICTORY
  //   แต่ถ้าหากผู้เล่นชนกำแพงครบ 5 ครั้งจะ GAMEOVER
  //   เมื่อเปิดเกมขึ้นมา หลังทำการกด simulate และ ticks enabled แล้ว กดปุ่ม start 
  //   ใช้คีย์บอร์ดในการควบคุมทิศทางดังต่อไปนี้   w (เดินขึ้น) s (เดินลง) a (เดินซ้าย) d (เดินขวา)  
endmodule

module stage1 (
  input  in_1,
  input  [2:0] in_2,
  input  [6:0] in_3,
  output [2:0] out_4,
  output [19:0] out_5,
  output [19:0] out_6,
  output [19:0] out_7,
  output [19:0] out_8,
  output [19:0] out_9,
  output [19:0] out_10,
  output [19:0] out_11,
  output [19:0] out_12,
  output [19:0] out_13,
  output [19:0] out_14,
  output [19:0] out_15,
  output [19:0] out_16,
  output [19:0] out_17,
  output [19:0] out_18,
  output [19:0] out_19,
  output [19:0] out_20,
  output [19:0] out_21,
  output [19:0] out_22,
  output [19:0] out_23,
  output [19:0] out_24,
  output [19:0] out_25,
  output [19:0] out_26,
  output [19:0] out_27,
  output [19:0] out_28,
  output [19:0] out_29,
  output out_30
);

  wire a, and_11_out, and_12_out, and_13_out, and_14_out, and_15_out, and_16_out, and_17_out, and_18_out,
       and_19_out, and_29_out, and_30_out, and_31_out, and_32_out, and_33_out, and_34_out, and_35_out,
       and_36_out, and_45_out, and_46_out, and_47_out, and_48_out, and_49_out, and_50_out, and_51_out,
       and_52_out, cc, clk, comparator_2_eq, comparator_3_eq, comparator_4_eq, comparator_5_eq,
       comparator_6_eq, comparator_7_eq, comparator_8_eq, comparator_9_eq, comparator_10_eq,
       comparator_15_gt, comparator_16_eq, comparator_17_eq, comparator_18_eq, comparator_19_eq,
       comparator_20_eq, comparator_21_eq, comparator_22_eq, comparator_23_eq, comparator_24_eq,
       comparator_25_eq, comparator_26_eq, comparator_27_eq, comparator_28_eq, comparator_29_eq,
       comparator_30_eq, comparator_31_eq, d, multiplexer_11_out, not_1_out, not_2_out, put, s, temp_clk,
       undriven, undriven_2, undriven_3, undriven_4, undriven_5, w;
  wire [1:0] and_10_out;
  wire [2:0] multiplexer_1_out, multiplexer_12_out;
  wire [3:0] adder_3_out, ss;
  wire [6:0] keyboard;
  wire [8:0] aa, adder_1_out, adder_2_out, bb, multiplexer_14_out, multiplexer_15_out, multiplexer_16_out,
       multiplexer_25_out, multiplexer_26_out, multiplexer_27_out, startx, starty, subtractor_1_out,
       subtractor_2_out, tempx, tempy, xx, yy;
  wire [19:0] and_1_out, and_2_out, and_3_out, and_4_out, and_5_out, and_6_out, and_7_out, and_8_out,
       and_9_out, and_21_out, and_22_out, and_23_out, and_24_out, and_25_out, and_26_out, and_27_out,
       and_28_out, and_37_out, and_38_out, and_39_out, and_40_out, and_41_out, and_42_out, and_43_out,
       and_44_out, rom_1_data, rom_2_data, rom_3_data, rom_4_data, rom_5_data, rom_6_data, rom_7_data,
       rom_8_data, rom_9_data, rom_10_data, rom_11_data, rom_12_data, rom_13_data, rom_14_data, rom_15_data,
       rom_16_data, rom_17_data, rom_18_data, rom_20_data, rom_21_data, rom_22_data, rom_23_data,
       rom_24_data, rom_25_data, rom_26_data, rom_27_data, zz;

  Clock clock_1 (.out(clk));
  ROM #(.addrWidth(5), .dataWidth(20)) rom_1 (.addr({5{1'b0}}), .data(rom_1_data));  // open: sel
  assign and_1_out = rom_1_data & zz;  // AND_Gate and_1, 20 bits wide
  ROM #(.addrWidth(5), .dataWidth(20)) rom_2 (.addr(5'b00011), .data(rom_2_data));  // open: sel
  assign and_2_out = rom_2_data & zz;  // AND_Gate and_2, 20 bits wide
  ROM #(.addrWidth(5), .dataWidth(20)) rom_3 (.addr(5'b00110), .data(rom_3_data));  // open: sel
  assign and_3_out = rom_3_data & zz;  // AND_Gate and_3, 20 bits wide
  ROM #(.addrWidth(5), .dataWidth(20)) rom_4 (.addr(5'b01001), .data(rom_4_data));  // open: sel
  assign and_4_out = rom_4_data & zz;  // AND_Gate and_4, 20 bits wide
  ROM #(.addrWidth(5), .dataWidth(20)) rom_5 (.addr(5'b01100), .data(rom_5_data));  // open: sel
  assign and_5_out = rom_5_data & zz;  // AND_Gate and_5, 20 bits wide
  ROM #(.addrWidth(5), .dataWidth(20)) rom_6 (.addr(5'b01111), .data(rom_6_data));  // open: sel
  assign and_6_out = rom_6_data & zz;  // AND_Gate and_6, 20 bits wide
  ROM #(.addrWidth(5), .dataWidth(20)) rom_7 (.addr(5'b10010), .data(rom_7_data));  // open: sel
  assign and_7_out = rom_7_data & zz;  // AND_Gate and_7, 20 bits wide
  ROM #(.addrWidth(5), .dataWidth(20)) rom_8 (.addr(5'b10101), .data(rom_8_data));  // open: sel
  assign and_8_out = rom_8_data & zz;  // AND_Gate and_8, 20 bits wide
  ROM #(.addrWidth(5), .dataWidth(20)) rom_9 (.addr(5'b11000), .data(rom_9_data));  // open: sel
  assign and_9_out = rom_9_data & zz;  // AND_Gate and_9, 20 bits wide
  Comparator #(.width(9)) comparator_1 (.a(aa), .b(9'h1e8), .eq(and_10_out[1]));  // open: gt, lt
  ROM #(.addrWidth(9), .dataWidth(20)) rom_10 (.addr(yy), .data(rom_10_data));  // open: sel
  Multiplexer #(.select(2), .width(3)) multiplexer_1 (
    .in0(out_4), .in1(3'b100), .in2(3'b001), .in3(out_4), .out(multiplexer_1_out), .sel(and_10_out));  // open: en
  and and_10 (and_10_out[0], not_1_out, comparator_15_gt);
  not not_1 (not_1_out, cc);
  not not_2 (not_2_out, cc);
  assign zz = ~rom_10_data;  // NOT_Gate not_3, 20 bits wide
  Multiplexer #(.width(20)) multiplexer_2 (
    .in0(rom_1_data), .in1(and_1_out), .out(out_5), .sel(and_11_out));  // open: en
  and and_11 (and_11_out, comparator_2_eq, temp_clk);
  Comparator #(.width(9)) comparator_2 (.a(xx), .b({9{1'b0}}), .eq(comparator_2_eq));  // open: gt, lt
  Multiplexer #(.width(20)) multiplexer_3 (
    .in0(rom_2_data), .in1(and_2_out), .out(out_8), .sel(and_12_out));  // open: en
  and and_12 (and_12_out, comparator_3_eq, temp_clk);
  Comparator #(.width(9)) comparator_3 (.a(xx), .b(9'h3), .eq(comparator_3_eq));  // open: gt, lt
  Multiplexer #(.width(20)) multiplexer_4 (
    .in0(rom_3_data), .in1(and_3_out), .out(out_11), .sel(and_13_out));  // open: en
  and and_13 (and_13_out, comparator_4_eq, temp_clk);
  Comparator #(.width(9)) comparator_4 (.a(xx), .b(9'h6), .eq(comparator_4_eq));  // open: gt, lt
  Multiplexer #(.width(20)) multiplexer_5 (
    .in0(rom_4_data), .in1(and_4_out), .out(out_14), .sel(and_14_out));  // open: en
  and and_14 (and_14_out, comparator_5_eq, temp_clk);
  Comparator #(.width(9)) comparator_5 (.a(xx), .b(9'h9), .eq(comparator_5_eq));  // open: gt, lt
  Multiplexer #(.width(20)) multiplexer_6 (
    .in0(rom_5_data), .in1(and_5_out), .out(out_17), .sel(and_15_out));  // open: en
  and and_15 (and_15_out, comparator_6_eq, temp_clk);
  Comparator #(.width(9)) comparator_6 (.a(xx), .b(9'hc), .eq(comparator_6_eq));  // open: gt, lt
  Multiplexer #(.width(20)) multiplexer_7 (
    .in0(rom_6_data), .in1(and_6_out), .out(out_20), .sel(and_16_out));  // open: en
  and and_16 (and_16_out, comparator_7_eq, temp_clk);
  Comparator #(.width(9)) comparator_7 (.a(xx), .b(9'hf), .eq(comparator_7_eq));  // open: gt, lt
  Multiplexer #(.width(20)) multiplexer_8 (
    .in0(rom_7_data), .in1(and_7_out), .out(out_23), .sel(and_17_out));  // open: en
  and and_17 (and_17_out, comparator_8_eq, temp_clk);
  Comparator #(.width(9)) comparator_8 (.a(xx), .b(9'h12), .eq(comparator_8_eq));  // open: gt, lt
  Multiplexer #(.width(20)) multiplexer_9 (
    .in0(rom_8_data), .in1(and_8_out), .out(out_26), .sel(and_18_out));  // open: en
  and and_18 (and_18_out, comparator_9_eq, temp_clk);
  Comparator #(.width(9)) comparator_9 (.a(xx), .b(9'h15), .eq(comparator_9_eq));  // open: gt, lt
  Multiplexer #(.width(20)) multiplexer_10 (
    .in0(rom_9_data), .in1(and_9_out), .out(out_29), .sel(and_19_out));  // open: en
  and and_19 (and_19_out, comparator_10_eq, temp_clk);
  Comparator #(.width(9)) comparator_10 (.a(xx), .b(9'h18), .eq(comparator_10_eq));  // open: gt, lt
  Comparator #(.width(7)) comparator_11 (.a(keyboard), .b(7'b1100001), .eq(a));  // open: gt, lt
  Comparator #(.width(7)) comparator_12 (.a(keyboard), .b(7'b1110111), .eq(w));  // open: gt, lt
  Comparator #(.width(7)) comparator_13 (.a(keyboard), .b(7'b1110011), .eq(s));  // open: gt, lt
  Comparator #(.width(7)) comparator_14 (.a(keyboard), .b(7'b1100100), .eq(d));  // open: gt, lt
  Comparator #(.width(9)) comparator_15 (.a(aa), .b({9{1'b0}}), .gt(comparator_15_gt));  // open: eq, lt
  Multiplexer multiplexer_11 (.in0(1'b0), .in1(1'b1), .out(multiplexer_11_out), .sel(not_2_out));  // open: en
  Subtractor #(.width(9)) subtractor_1 (.a(aa), .b(9'h1), .out(subtractor_1_out));  // open: bin, bout
  Subtractor #(.width(9)) subtractor_2 (.a(aa), .b(9'h14), .out(subtractor_2_out));  // open: bin, bout
  Adder #(.width(9)) adder_1 (.a(aa), .b(9'h14), .out(adder_1_out));  // open: cin, cout
  Adder #(.width(9)) adder_2 (.a(aa), .b(9'h1), .out(adder_2_out));  // open: cin, cout
  Register #(.width(3)) register_1 (.D(multiplexer_12_out), .Q(out_4), .clk(clk), .clr(undriven_2));  // open: en
  Multiplexer #(.width(3)) multiplexer_12 (
    .in0(multiplexer_1_out), .in1(in_2), .out(multiplexer_12_out), .sel(in_1));  // open: en
  Register #(.width(1)) register_2 (.D(multiplexer_11_out), .Q(out_30), .clk(clk), .clr(undriven));  // open: en
  TTY tty_1 (.data(in_3), .clk(clk));  // open: we, clr
  and and_20 (put, d, s, w, a);
  Multiplexer #(.select(4), .width(9)) multiplexer_13 (
    .in0(aa), .in1(subtractor_1_out), .in2(subtractor_2_out), .in3(aa), .in4(adder_1_out), .in5(aa),
    .in6(aa), .in7(aa), .in8(adder_2_out), .in9(aa), .in10(aa), .in11(aa), .in12(aa), .in13(aa), .in14(aa),
    .in15(aa), .out(bb), .sel({d, s, w, a}));  // open: en
  ROM #(.addrWidth(5), .dataWidth(20)) rom_11 (.addr(5'b00001), .data(rom_11_data));  // open: sel
  assign and_21_out = rom_11_data & zz;  // AND_Gate and_21, 20 bits wide
  ROM #(.addrWidth(5), .dataWidth(20)) rom_12 (.addr(5'b00100), .data(rom_12_data));  // open: sel
  assign and_22_out = rom_12_data & zz;  // AND_Gate and_22, 20 bits wide
  ROM #(.addrWidth(5), .dataWidth(20)) rom_13 (.addr(5'b00111), .data(rom_13_data));  // open: sel
  assign and_23_out = rom_13_data & zz;  // AND_Gate and_23, 20 bits wide
  ROM #(.addrWidth(5), .dataWidth(20)) rom_14 (.addr(5'b01010), .data(rom_14_data));  // open: sel
  assign and_24_out = rom_14_data & zz;  // AND_Gate and_24, 20 bits wide
  ROM #(.addrWidth(5), .dataWidth(20)) rom_15 (.addr(5'b01101), .data(rom_15_data));  // open: sel
  assign and_25_out = rom_15_data & zz;  // AND_Gate and_25, 20 bits wide
  ROM #(.addrWidth(5), .dataWidth(20)) rom_16 (.addr(5'b10000), .data(rom_16_data));  // open: sel
  assign and_26_out = rom_16_data & zz;  // AND_Gate and_26, 20 bits wide
  ROM #(.addrWidth(5), .dataWidth(20)) rom_17 (.addr(5'b10011), .data(rom_17_data));  // open: sel
  assign and_27_out = rom_17_data & zz;  // AND_Gate and_27, 20 bits wide
  ROM #(.addrWidth(5), .dataWidth(20)) rom_18 (.addr(5'b10110), .data(rom_18_data));  // open: sel
  assign and_28_out = rom_18_data & zz;  // AND_Gate and_28, 20 bits wide
  Multiplexer #(.width(9)) multiplexer_14 (.in0(yy), .in1(tempy), .out(multiplexer_14_out), .sel(cc));  // open: en
  Multiplexer #(.width(9)) multiplexer_15 (.in0(xx), .in1(tempx), .out(multiplexer_15_out), .sel(cc));  // open: en
  Multiplexer #(.width(9)) multiplexer_16 (.in0(aa), .in1(bb), .out(multiplexer_16_out), .sel(cc));  // open: en
  Multiplexer #(.width(20)) multiplexer_17 (
    .in0(rom_11_data), .in1(and_21_out), .out(out_6), .sel(and_29_out));  // open: en
  and and_29 (and_29_out, comparator_16_eq, temp_clk);
  Comparator #(.width(9)) comparator_16 (.a(xx), .b(9'h1), .eq(comparator_16_eq));  // open: gt, lt
  Multiplexer #(.width(20)) multiplexer_18 (
    .in0(rom_12_data), .in1(and_22_out), .out(out_9), .sel(and_30_out));  // open: en
  and and_30 (and_30_out, comparator_17_eq, temp_clk);
  Comparator #(.width(9)) comparator_17 (.a(xx), .b(9'h4), .eq(comparator_17_eq));  // open: gt, lt
  Multiplexer #(.width(20)) multiplexer_19 (
    .in0(rom_13_data), .in1(and_23_out), .out(out_12), .sel(and_31_out));  // open: en
  and and_31 (and_31_out, comparator_18_eq, temp_clk);
  Comparator #(.width(9)) comparator_18 (.a(xx), .b(9'h7), .eq(comparator_18_eq));  // open: gt, lt
  Multiplexer #(.width(20)) multiplexer_20 (
    .in0(rom_14_data), .in1(and_24_out), .out(out_15), .sel(and_32_out));  // open: en
  and and_32 (and_32_out, comparator_19_eq, temp_clk);
  Comparator #(.width(9)) comparator_19 (.a(xx), .b(9'ha), .eq(comparator_19_eq));  // open: gt, lt
  Multiplexer #(.width(20)) multiplexer_21 (
    .in0(rom_15_data), .in1(and_25_out), .out(out_18), .sel(and_33_out));  // open: en
  and and_33 (and_33_out, comparator_20_eq, temp_clk);
  Comparator #(.width(9)) comparator_20 (.a(xx), .b(9'hd), .eq(comparator_20_eq));  // open: gt, lt
  Multiplexer #(.width(20)) multiplexer_22 (
    .in0(rom_16_data), .in1(and_26_out), .out(out_21), .sel(and_34_out));  // open: en
  and and_34 (and_34_out, comparator_21_eq, temp_clk);
  Comparator #(.width(9)) comparator_21 (.a(xx), .b(9'h10), .eq(comparator_21_eq));  // open: gt, lt
  Multiplexer #(.width(20)) multiplexer_23 (
    .in0(rom_17_data), .in1(and_27_out), .out(out_24), .sel(and_35_out));  // open: en
  and and_35 (and_35_out, comparator_22_eq, temp_clk);
  Comparator #(.width(9)) comparator_22 (.a(xx), .b(9'h13), .eq(comparator_22_eq));  // open: gt, lt
  Multiplexer #(.width(20)) multiplexer_24 (
    .in0(rom_18_data), .in1(and_28_out), .out(out_27), .sel(and_36_out));  // open: en
  and and_36 (and_36_out, comparator_23_eq, temp_clk);
  Comparator #(.width(9)) comparator_23 (.a(xx), .b(9'h16), .eq(comparator_23_eq));  // open: gt, lt
  Multiplexer #(.width(9)) multiplexer_25 (
    .in0(multiplexer_16_out), .in1(9'h8), .out(multiplexer_25_out), .sel(in_1));  // open: en
  Divider #(.width(9)) divider_1 (.a(bb), .b(9'h14), .out(tempx), .rem(tempy));  // open: upper
  Divider #(.width(9)) divider_2 (.a(9'h8), .b(9'h14), .out(startx), .rem(starty));  // open: upper
  Register #(.width(9)) register_3 (.D(multiplexer_26_out), .Q(yy), .clk(clk), .clr(undriven_3));  // open: en
  Multiplexer #(.width(9)) multiplexer_26 (
    .in0(multiplexer_14_out), .in1(starty), .out(multiplexer_26_out), .sel(in_1));  // open: en
  Register #(.width(9)) register_4 (.D(multiplexer_27_out), .Q(xx), .clk(clk), .clr(undriven_4));  // open: en
  Multiplexer #(.width(9)) multiplexer_27 (
    .in0(multiplexer_15_out), .in1(startx), .out(multiplexer_27_out), .sel(in_1));  // open: en
  Adder #(.width(4)) adder_3 (.a(ss), .b(4'b0001), .out(adder_3_out));  // open: cin, cout
  Register #(.width(9)) register_5 (.D(multiplexer_25_out), .Q(aa), .clk(clk), .clr(undriven_5));  // open: en
  ROM #(.addrWidth(9), .dataWidth(1)) rom_19 (.addr(bb), .data(cc));  // open: sel
  Register #(.width(4)) register_6 (.D(adder_3_out), .Q(ss), .clk(clk), .clr(put));  // open: en
  Multiplexer #(.select(4)) multiplexer_28 (
    .in0(1'b0), .in1(1'b0), .in2(1'b0), .in3(1'b0), .in4(1'b0), .in5(1'b0), .in6(1'b0), .in7(1'b1),
    .in8(1'b1), .in9(1'b1), .in10(1'b1), .in11(1'b1), .in12(1'b1), .in13(1'b1), .in14(1'b1), .in15(1'b1),
    .out(temp_clk), .sel(ss));  // open: en
  ROM #(.addrWidth(5), .dataWidth(20)) rom_20 (.addr(5'b00010), .data(rom_20_data));  // open: sel
  assign and_37_out = rom_20_data & zz;  // AND_Gate and_37, 20 bits wide
  ROM #(.addrWidth(5), .dataWidth(20)) rom_21 (.addr(5'b00101), .data(rom_21_data));  // open: sel
  assign and_38_out = rom_21_data & zz;  // AND_Gate and_38, 20 bits wide
  ROM #(.addrWidth(5), .dataWidth(20)) rom_22 (.addr(5'b01000), .data(rom_22_data));  // open: sel
  assign and_39_out = rom_22_data & zz;  // AND_Gate and_39, 20 bits wide
  ROM #(.addrWidth(5), .dataWidth(20)) rom_23 (.addr(5'b01011), .data(rom_23_data));  // open: sel
  assign and_40_out = rom_23_data & zz;  // AND_Gate and_40, 20 bits wide
  ROM #(.addrWidth(5), .dataWidth(20)) rom_24 (.addr(5'b01110), .data(rom_24_data));  // open: sel
  assign and_41_out = rom_24_data & zz;  // AND_Gate and_41, 20 bits wide
  ROM #(.addrWidth(5), .dataWidth(20)) rom_25 (.addr(5'b10001), .data(rom_25_data));  // open: sel
  assign and_42_out = rom_25_data & zz;  // AND_Gate and_42, 20 bits wide
  ROM #(.addrWidth(5), .dataWidth(20)) rom_26 (.addr(5'b10100), .data(rom_26_data));  // open: sel
  assign and_43_out = rom_26_data & zz;  // AND_Gate and_43, 20 bits wide
  ROM #(.addrWidth(5), .dataWidth(20)) rom_27 (.addr(5'b10111), .data(rom_27_data));  // open: sel
  assign and_44_out = rom_27_data & zz;  // AND_Gate and_44, 20 bits wide
  Comparator #(.width(9)) comparator_24 (.a(xx), .b(9'h2), .eq(comparator_24_eq));  // open: gt, lt
  Comparator #(.width(9)) comparator_25 (.a(xx), .b(9'h5), .eq(comparator_25_eq));  // open: gt, lt
  Comparator #(.width(9)) comparator_26 (.a(xx), .b(9'h8), .eq(comparator_26_eq));  // open: gt, lt
  Comparator #(.width(9)) comparator_27 (.a(xx), .b(9'hb), .eq(comparator_27_eq));  // open: gt, lt
  Comparator #(.width(9)) comparator_28 (.a(xx), .b(9'he), .eq(comparator_28_eq));  // open: gt, lt
  Comparator #(.width(9)) comparator_29 (.a(xx), .b(9'h11), .eq(comparator_29_eq));  // open: gt, lt
  Multiplexer #(.width(20)) multiplexer_29 (
    .in0(rom_26_data), .in1(and_43_out), .out(out_25), .sel(and_51_out));  // open: en
  Comparator #(.width(9)) comparator_30 (.a(xx), .b(9'h14), .eq(comparator_30_eq));  // open: gt, lt
  Multiplexer #(.width(20)) multiplexer_30 (
    .in0(rom_27_data), .in1(and_44_out), .out(out_28), .sel(and_52_out));  // open: en
  Comparator #(.width(9)) comparator_31 (.a(xx), .b(9'h17), .eq(comparator_31_eq));  // open: gt, lt
  Multiplexer #(.width(20)) multiplexer_31 (
    .in0(rom_20_data), .in1(and_37_out), .out(out_7), .sel(and_45_out));  // open: en
  and and_45 (and_45_out, comparator_24_eq, temp_clk);
  Multiplexer #(.width(20)) multiplexer_32 (
    .in0(rom_21_data), .in1(and_38_out), .out(out_10), .sel(and_46_out));  // open: en
  and and_46 (and_46_out, comparator_25_eq, temp_clk);
  Multiplexer #(.width(20)) multiplexer_33 (
    .in0(rom_22_data), .in1(and_39_out), .out(out_13), .sel(and_47_out));  // open: en
  and and_47 (and_47_out, comparator_26_eq, temp_clk);
  Multiplexer #(.width(20)) multiplexer_34 (
    .in0(rom_23_data), .in1(and_40_out), .out(out_16), .sel(and_48_out));  // open: en
  and and_48 (and_48_out, comparator_27_eq, temp_clk);
  Multiplexer #(.width(20)) multiplexer_35 (
    .in0(rom_24_data), .in1(and_41_out), .out(out_19), .sel(and_49_out));  // open: en
  and and_49 (and_49_out, comparator_28_eq, temp_clk);
  Multiplexer #(.width(20)) multiplexer_36 (
    .in0(rom_25_data), .in1(and_42_out), .out(out_22), .sel(and_50_out));  // open: en
  and and_50 (and_50_out, comparator_29_eq, temp_clk);
  and and_51 (and_51_out, comparator_30_eq, temp_clk);
  and and_52 (and_52_out, comparator_31_eq, temp_clk);

  // Other names for the same wires on the sheet: ggg = out_30; keyboard_t[6:0] = in_3; reset = in_1;
  //   stage[2:0] = out_4; thisstage[2:0] = in_2

  // Notes on the sheet:
  //   contents of rom_1 (hex, n*v repeats v):
  //   800 7bcea 4e18e 60cda 3e652 2b376 619e0 cc2e 7fdfa 782 7f03e 5fe4 7c46e 45f04 5c87c 51bd6 5d052
  //   11fda 55092 47aba 5c388 51eee 5c822 76bee 800
  //   contents of rom_2 (hex, n*v repeats v):
  //   800 7bcea 4e18e 60cda 3e652 2b376 619e0 cc2e 7fdfa 782 7f03e 5fe4 7c46e 45f04 5c87c 51bd6 5d052
  //   11fda 55092 47aba 5c388 51eee 5c822 76bee 800
  //   contents of rom_3 (hex, n*v repeats v):
  //   800 7bcea 4e18e 60cda 3e652 2b376 619e0 cc2e 7fdfa 782 7f03e 5fe4 7c46e 45f04 5c87c 51bd6 5d052
  //   11fda 55092 47aba 5c388 51eee 5c822 76bee 800
  //   contents of rom_4 (hex, n*v repeats v):
  //   800 7bcea 4e18e 60cda 3e652 2b376 619e0 cc2e 7fdfa 782 7f03e 5fe4 7c46e 45f04 5c87c 51bd6 5d052
  //   11fda 55092 47aba 5c388 51eee 5c822 76bee 800
  //   contents of rom_5 (hex, n*v repeats v):
  //   800 7bcea 4e18e 60cda 3e652 2b376 619e0 cc2e 7fdfa 782 7f03e 5fe4 7c46e 45f04 5c87c 51bd6 5d052
  //   11fda 55092 47aba 5c388 51eee 5c822 76bee 800
  //   contents of rom_6 (hex, n*v repeats v):
  //   800 7bcea 4e18e 60cda 3e652 2b376 619e0 cc2e 7fdfa 782 7f03e 5fe4 7c46e 45f04 5c87c 51bd6 5d052
  //   11fda 55092 47aba 5c388 51eee 5c822 76bee 800
  //   contents of rom_7 (hex, n*v repeats v):
  //   800 7bcea 4e18e 60cda 3e652 2b376 619e0 cc2e 7fdfa 782 7f03e 5fe4 7c46e 45f04 5c87c 51bd6 5d052
  //   11fda 55092 47aba 5c388 51eee 5c822 76bee 800
  //   contents of rom_8 (hex, n*v repeats v):
  //   800 7bcea 4e18e 60cda 3e652 2b376 619e0 cc2e 7fdfa 782 7f03e 5fe4 7c46e 45f04 5c87c 51bd6 5d052
  //   11fda 55092 47aba 5c388 51eee 5c822 76bee 800
  //   contents of rom_9 (hex, n*v repeats v):
  //   800 7bcea 4e18e 60cda 3e652 2b376 619e0 cc2e 7fdfa 782 7f03e 5fe4 7c46e 45f04 5c87c 51bd6 5d052
  //   11fda 55092 47aba 5c388 51eee 5c822 76bee 800
  //   contents of rom_10 (hex, n*v repeats v):
  //   80000 40000 20000 10000 8000 4000 2000 1000 800 400 200 100 80 40 20 10 8 4 2 1 4*0 800
  //   a
  //   w
  //   s
  //   d
  //   contents of rom_11 (hex, n*v repeats v):
  //   800 7bcea 4e18e 60cda 3e652 2b376 619e0 cc2e 7fdfa 782 7f03e 5fe4 7c46e 45f04 5c87c 51bd6 5d052
  //   11fda 55092 47aba 5c388 51eee 5c822 76bee 800
  //   contents of rom_12 (hex, n*v repeats v):
  //   800 7bcea 4e18e 60cda 3e652 2b376 619e0 cc2e 7fdfa 782 7f03e 5fe4 7c46e 45f04 5c87c 51bd6 5d052
  //   11fda 55092 47aba 5c388 51eee 5c822 76bee 800
  //   contents of rom_13 (hex, n*v repeats v):
  //   800 7bcea 4e18e 60cda 3e652 2b376 619e0 cc2e 7fdfa 782 7f03e 5fe4 7c46e 45f04 5c87c 51bd6 5d052
  //   11fda 55092 47aba 5c388 51eee 5c822 76bee 800
  //   contents of rom_14 (hex, n*v repeats v):
  //   800 7bcea 4e18e 60cda 3e652 2b376 619e0 cc2e 7fdfa 782 7f03e 5fe4 7c46e 45f04 5c87c 51bd6 5d052
  //   11fda 55092 47aba 5c388 51eee 5c822 76bee 800
  //   contents of rom_15 (hex, n*v repeats v):
  //   800 7bcea 4e18e 60cda 3e652 2b376 619e0 cc2e 7fdfa 782 7f03e 5fe4 7c46e 45f04 5c87c 51bd6 5d052
  //   11fda 55092 47aba 5c388 51eee 5c822 76bee 800
  //   contents of rom_16 (hex, n*v repeats v):
  //   800 7bcea 4e18e 60cda 3e652 2b376 619e0 cc2e 7fdfa 782 7f03e 5fe4 7c46e 45f04 5c87c 51bd6 5d052
  //   11fda 55092 47aba 5c388 51eee 5c822 76bee 800
  //   contents of rom_17 (hex, n*v repeats v):
  //   800 7bcea 4e18e 60cda 3e652 2b376 619e0 cc2e 7fdfa 782 7f03e 5fe4 7c46e 45f04 5c87c 51bd6 5d052
  //   11fda 55092 47aba 5c388 51eee 5c822 76bee 800
  //   contents of rom_18 (hex, n*v repeats v):
  //   800 7bcea 4e18e 60cda 3e652 2b376 619e0 cc2e 7fdfa 782 7f03e 5fe4 7c46e 45f04 5c87c 51bd6 5d052
  //   11fda 55092 47aba 5c388 51eee 5c822 76bee 800
  //   contents of rom_19 (hex, n*v repeats v):
  //   8*0 1 12*0 4*1 0 4*1 0 0 1 1 1 0 1 0 1 0 0 1 0 0 1 1 1 4*0 1 1 0 0 0 1 1 1 0 0 1 1 5*0 1 1 0 0 1 1 0
  //   1 1 0 1 0 0 0 5*1 0 0 1 1 0 0 1 0 1 0 0 1 0 0 0 1 0 1 0 1 1 0 0 1 1 0 1 1 1 0 1 1 0 0 1 1 4*0 1 1 0
  //   0 4*1 9*0 1 1 0 0 1 1 4*0 1 0 1 1 1 0 0 9*1 0 6*1 0 1 10*0 4*1 5*0 1 0 0 7*1 6*0 5*1 6*0 1 0 8*1 0 0
  //   1 0 0 0 5*1 0 0 0 1 0 0 0 1 1 0 1 1 1 0 0 1 0 0 0 1 0 5*1 5*0 1 0 0 0 1 0 1 1 1 0 0 1 4*0 5*1 0 0 0
  //   1 0 1 0 0 0 1 1 0 4*1 0 1 0 1 1 0 0 1 0 1 1 1 0 1 5*0 1 0 1 0 0 1 4*0 1 0 0 0 7*1 0 1 1 0 1 0 0 1 0
  //   1 0 1 0 1 4*0 1 0 0 1 0 0 1 0 0 1 0 0 0 4*1 0 1 0 1 0 1 1 1 0 1 0 0 1 0 1 1 1 4*0 1 1 1 0 0 0 1 4*0
  //   1 0 1 0 0 0 4*1 0 1 1 1 0 1 1 1 0 0 1 0 1 1 1 0 0 1 5*0 1 0 0 0 1 0 0 1 1 1 0 1 1 0 1 0 5*1 0 1 1 1
  //   9*0 1
  //   contents of rom_20 (hex, n*v repeats v):
  //   800 7bcea 4e18e 60cda 3e652 2b376 619e0 cc2e 7fdfa 782 7f03e 5fe4 7c46e 45f04 5c87c 51bd6 5d052
  //   11fda 55092 47aba 5c388 51eee 5c822 76bee 800
  //   contents of rom_21 (hex, n*v repeats v):
  //   800 7bcea 4e18e 60cda 3e652 2b376 619e0 cc2e 7fdfa 782 7f03e 5fe4 7c46e 45f04 5c87c 51bd6 5d052
  //   11fda 55092 47aba 5c388 51eee 5c822 76bee 800
  //   contents of rom_22 (hex, n*v repeats v):
  //   800 7bcea 4e18e 60cda 3e652 2b376 619e0 cc2e 7fdfa 782 7f03e 5fe4 7c46e 45f04 5c87c 51bd6 5d052
  //   11fda 55092 47aba 5c388 51eee 5c822 76bee 800
  //   contents of rom_23 (hex, n*v repeats v):
  //   800 7bcea 4e18e 60cda 3e652 2b376 619e0 cc2e 7fdfa 782 7f03e 5fe4 7c46e 45f04 5c87c 51bd6 5d052
  //   11fda 55092 47aba 5c388 51eee 5c822 76bee 800
  //   contents of rom_24 (hex, n*v repeats v):
  //   800 7bcea 4e18e 60cda 3e652 2b376 619e0 cc2e 7fdfa 782 7f03e 5fe4 7c46e 45f04 5c87c 51bd6 5d052
  //   11fda 55092 47aba 5c388 51eee 5c822 76bee 800
  //   contents of rom_25 (hex, n*v repeats v):
  //   800 7bcea 4e18e 60cda 3e652 2b376 619e0 cc2e 7fdfa 782 7f03e 5fe4 7c46e 45f04 5c87c 51bd6 5d052
  //   11fda 55092 47aba 5c388 51eee 5c822 76bee 800
  //   contents of rom_26 (hex, n*v repeats v):
  //   800 7bcea 4e18e 60cda 3e652 2b376 619e0 cc2e 7fdfa 782 7f03e 5fe4 7c46e 45f04 5c87c 51bd6 5d052
  //   11fda 55092 47aba 5c388 51eee 5c822 76bee 800
  //   contents of rom_27 (hex, n*v repeats v):
  //   800 7bcea 4e18e 60cda 3e652 2b376 619e0 cc2e 7fdfa 782 7f03e 5fe4 7c46e 45f04 5c87c 51bd6 5d052
  //   11fda 55092 47aba 5c388 51eee 5c822 76bee 800
endmodule

module stage2 (
  input  in_1,
  input  [2:0] in_2,
  input  [6:0] in_3,
  output [2:0] out_4,
  output [19:0] out_5,
  output [19:0] out_6,
  output [19:0] out_7,
  output [19:0] out_8,
  output [19:0] out_9,
  output [19:0] out_10,
  output [19:0] out_11,
  output [19:0] out_12,
  output [19:0] out_13,
  output [19:0] out_14,
  output [19:0] out_15,
  output [19:0] out_16,
  output [19:0] out_17,
  output [19:0] out_18,
  output [19:0] out_19,
  output [19:0] out_20,
  output [19:0] out_21,
  output [19:0] out_22,
  output [19:0] out_23,
  output [19:0] out_24,
  output [19:0] out_25,
  output [19:0] out_26,
  output [19:0] out_27,
  output [19:0] out_28,
  output [19:0] out_29,
  output out_30
);

  wire a, and_11_out, and_12_out, and_13_out, and_14_out, and_15_out, and_16_out, and_17_out, and_18_out,
       and_19_out, and_29_out, and_30_out, and_31_out, and_32_out, and_33_out, and_34_out, and_35_out,
       and_36_out, and_45_out, and_46_out, and_47_out, and_48_out, and_49_out, and_50_out, and_51_out,
       and_52_out, cc, clk, comparator_2_eq, comparator_3_eq, comparator_4_eq, comparator_5_eq,
       comparator_6_eq, comparator_7_eq, comparator_8_eq, comparator_9_eq, comparator_10_eq,
       comparator_15_gt, comparator_16_eq, comparator_17_eq, comparator_18_eq, comparator_19_eq,
       comparator_20_eq, comparator_21_eq, comparator_22_eq, comparator_23_eq, comparator_24_eq,
       comparator_25_eq, comparator_26_eq, comparator_27_eq, comparator_28_eq, comparator_29_eq,
       comparator_30_eq, comparator_31_eq, d, multiplexer_12_out, not_1_out, not_2_out, put, s, temp_clk,
       undriven, undriven_2, undriven_3, undriven_4, undriven_5, w;
  wire [1:0] and_10_out;
  wire [2:0] multiplexer_1_out, multiplexer_11_out;
  wire [3:0] adder_3_out, ss;
  wire [6:0] keyboard;
  wire [8:0] aa, adder_1_out, adder_2_out, bb, multiplexer_14_out, multiplexer_15_out, multiplexer_16_out,
       multiplexer_17_out, multiplexer_18_out, multiplexer_27_out, startx, starty, subtractor_1_out,
       subtractor_2_out, tempx, tempy, xx, yy;
  wire [19:0] and_1_out, and_2_out, and_3_out, and_4_out, and_5_out, and_6_out, and_7_out, and_8_out,
       and_9_out, and_21_out, and_22_out, and_23_out, and_24_out, and_25_out, and_26_out, and_27_out,
       and_28_out, and_37_out, and_38_out, and_39_out, and_40_out, and_41_out, and_42_out, and_43_out,
       and_44_out, rom_1_data, rom_2_data, rom_3_data, rom_4_data, rom_5_data, rom_6_data, rom_7_data,
       rom_8_data, rom_9_data, rom_10_data, rom_11_data, rom_12_data, rom_13_data, rom_14_data, rom_15_data,
       rom_16_data, rom_17_data, rom_18_data, rom_20_data, rom_21_data, rom_22_data, rom_23_data,
       rom_24_data, rom_25_data, rom_26_data, rom_27_data, zz;

  Clock clock_1 (.out(clk));
  ROM #(.addrWidth(5), .dataWidth(20)) rom_1 (.addr({5{1'b0}}), .data(rom_1_data));  // open: sel
  assign and_1_out = rom_1_data & zz;  // AND_Gate and_1, 20 bits wide
  ROM #(.addrWidth(5), .dataWidth(20)) rom_2 (.addr(5'b00011), .data(rom_2_data));  // open: sel
  assign and_2_out = rom_2_data & zz;  // AND_Gate and_2, 20 bits wide
  ROM #(.addrWidth(5), .dataWidth(20)) rom_3 (.addr(5'b00110), .data(rom_3_data));  // open: sel
  assign and_3_out = rom_3_data & zz;  // AND_Gate and_3, 20 bits wide
  ROM #(.addrWidth(5), .dataWidth(20)) rom_4 (.addr(5'b01001), .data(rom_4_data));  // open: sel
  assign and_4_out = rom_4_data & zz;  // AND_Gate and_4, 20 bits wide
  ROM #(.addrWidth(5), .dataWidth(20)) rom_5 (.addr(5'b01100), .data(rom_5_data));  // open: sel
  assign and_5_out = rom_5_data & zz;  // AND_Gate and_5, 20 bits wide
  ROM #(.addrWidth(5), .dataWidth(20)) rom_6 (.addr(5'b01111), .data(rom_6_data));  // open: sel
  assign and_6_out = rom_6_data & zz;  // AND_Gate and_6, 20 bits wide
  ROM #(.addrWidth(5), .dataWidth(20)) rom_7 (.addr(5'b10010), .data(rom_7_data));  // open: sel
  assign and_7_out = rom_7_data & zz;  // AND_Gate and_7, 20 bits wide
  ROM #(.addrWidth(5), .dataWidth(20)) rom_8 (.addr(5'b10101), .data(rom_8_data));  // open: sel
  assign and_8_out = rom_8_data & zz;  // AND_Gate and_8, 20 bits wide
  ROM #(.addrWidth(5), .dataWidth(20)) rom_9 (.addr(5'b11000), .data(rom_9_data));  // open: sel
  assign and_9_out = rom_9_data & zz;  // AND_Gate and_9, 20 bits wide
  Comparator #(.width(9)) comparator_1 (.a(aa), .b(9'h1e8), .eq(and_10_out[1]));  // open: gt, lt
  ROM #(.addrWidth(9), .dataWidth(20)) rom_10 (.addr(yy), .data(rom_10_data));  // open: sel
  Multiplexer #(.select(2), .width(3)) multiplexer_1 (
    .in0(out_4), .in1(3'b100), .in2(3'b010), .in3(out_4), .out(multiplexer_1_out), .sel(and_10_out));  // open: en
  and and_10 (and_10_out[0], not_1_out, comparator_15_gt);
  not not_1 (not_1_out, cc);
  not not_2 (not_2_out, cc);
  assign zz = ~rom_10_data;  // NOT_Gate not_3, 20 bits wide
  Multiplexer #(.width(20)) multiplexer_2 (
    .in0(rom_1_data), .in1(and_1_out), .out(out_5), .sel(and_11_out));  // open: en
  and and_11 (and_11_out, comparator_2_eq, temp_clk);
  Comparator #(.width(9)) comparator_2 (.a(xx), .b({9{1'b0}}), .eq(comparator_2_eq));  // open: gt, lt
  Multiplexer #(.width(20)) multiplexer_3 (
    .in0(rom_2_data), .in1(and_2_out), .out(out_8), .sel(and_12_out));  // open: en
  and and_12 (and_12_out, comparator_3_eq, temp_clk);
  Comparator #(.width(9)) comparator_3 (.a(xx), .b(9'h3), .eq(comparator_3_eq));  // open: gt, lt
  Multiplexer #(.width(20)) multiplexer_4 (
    .in0(rom_3_data), .in1(and_3_out), .out(out_11), .sel(and_13_out));  // open: en
  and and_13 (and_13_out, comparator_4_eq, temp_clk);
  Comparator #(.width(9)) comparator_4 (.a(xx), .b(9'h6), .eq(comparator_4_eq));  // open: gt, lt
  Multiplexer #(.width(20)) multiplexer_5 (
    .in0(rom_4_data), .in1(and_4_out), .out(out_14), .sel(and_14_out));  // open: en
  and and_14 (and_14_out, comparator_5_eq, temp_clk);
  Comparator #(.width(9)) comparator_5 (.a(xx), .b(9'h9), .eq(comparator_5_eq));  // open: gt, lt
  Multiplexer #(.width(20)) multiplexer_6 (
    .in0(rom_5_data), .in1(and_5_out), .out(out_17), .sel(and_15_out));  // open: en
  and and_15 (and_15_out, comparator_6_eq, temp_clk);
  Comparator #(.width(9)) comparator_6 (.a(xx), .b(9'hc), .eq(comparator_6_eq));  // open: gt, lt
  Multiplexer #(.width(20)) multiplexer_7 (
    .in0(rom_6_data), .in1(and_6_out), .out(out_20), .sel(and_16_out));  // open: en
  and and_16 (and_16_out, comparator_7_eq, temp_clk);
  Comparator #(.width(9)) comparator_7 (.a(xx), .b(9'hf), .eq(comparator_7_eq));  // open: gt, lt
  Multiplexer #(.width(20)) multiplexer_8 (
    .in0(rom_7_data), .in1(and_7_out), .out(out_23), .sel(and_17_out));  // open: en
  and and_17 (and_17_out, comparator_8_eq, temp_clk);
  Comparator #(.width(9)) comparator_8 (.a(xx), .b(9'h12), .eq(comparator_8_eq));  // open: gt, lt
  Multiplexer #(.width(20)) multiplexer_9 (
    .in0(rom_8_data), .in1(and_8_out), .out(out_26), .sel(and_18_out));  // open: en
  and and_18 (and_18_out, comparator_9_eq, temp_clk);
  Comparator #(.width(9)) comparator_9 (.a(xx), .b(9'h15), .eq(comparator_9_eq));  // open: gt, lt
  Multiplexer #(.width(20)) multiplexer_10 (
    .in0(rom_9_data), .in1(and_9_out), .out(out_29), .sel(and_19_out));  // open: en
  and and_19 (and_19_out, comparator_10_eq, temp_clk);
  Comparator #(.width(9)) comparator_10 (.a(xx), .b(9'h18), .eq(comparator_10_eq));  // open: gt, lt
  Subtractor #(.width(9)) subtractor_1 (.a(aa), .b(9'h1), .out(subtractor_1_out));  // open: bin, bout
  Subtractor #(.width(9)) subtractor_2 (.a(aa), .b(9'h14), .out(subtractor_2_out));  // open: bin, bout
  Adder #(.width(9)) adder_1 (.a(aa), .b(9'h14), .out(adder_1_out));  // open: cin, cout
  Adder #(.width(9)) adder_2 (.a(aa), .b(9'h1), .out(adder_2_out));  // open: cin, cout
  Comparator #(.width(7)) comparator_11 (.a(keyboard), .b(7'b1100001), .eq(a));  // open: gt, lt
  Comparator #(.width(7)) comparator_12 (.a(keyboard), .b(7'b1110111), .eq(w));  // open: gt, lt
  Comparator #(.width(7)) comparator_13 (.a(keyboard), .b(7'b1110011), .eq(s));  // open: gt, lt
  Comparator #(.width(7)) comparator_14 (.a(keyboard), .b(7'b1100100), .eq(d));  // open: gt, lt
  Multiplexer #(.width(3)) multiplexer_11 (
    .in0(multiplexer_1_out), .in1(in_2), .out(multiplexer_11_out), .sel(in_1));  // open: en
  Comparator #(.width(9)) comparator_15 (.a(aa), .b({9{1'b0}}), .gt(comparator_15_gt));  // open: eq, lt
  Multiplexer multiplexer_12 (.in0(1'b0), .in1(1'b1), .out(multiplexer_12_out), .sel(not_2_out));  // open: en
  Register #(.width(3)) register_1 (.D(multiplexer_11_out), .Q(out_4), .clk(clk), .clr(undriven_2));  // open: en
  Register #(.width(1)) register_2 (.D(multiplexer_12_out), .Q(out_30), .clk(clk), .clr(undriven));  // open: en
  TTY tty_1 (.data(in_3), .clk(clk));  // open: we, clr
  and and_20 (put, d, s, w, a);
  Multiplexer #(.select(4), .width(9)) multiplexer_13 (
    .in0(aa), .in1(subtractor_1_out), .in2(subtractor_2_out), .in3(aa), .in4(adder_1_out), .in5(aa),
    .in6(aa), .in7(aa), .in8(adder_2_out), .in9(aa), .in10(aa), .in11(aa), .in12(aa), .in13(aa), .in14(aa),
    .in15(aa), .out(bb), .sel({d, s, w, a}));  // open: en
  ROM #(.addrWidth(5), .dataWidth(20)) rom_11 (.addr(5'b00001), .data(rom_11_data));  // open: sel
  assign and_21_out = rom_11_data & zz;  // AND_Gate and_21, 20 bits wide
  ROM #(.addrWidth(5), .dataWidth(20)) rom_12 (.addr(5'b00100), .data(rom_12_data));  // open: sel
  assign and_22_out = rom_12_data & zz;  // AND_Gate and_22, 20 bits wide
  ROM #(.addrWidth(5), .dataWidth(20)) rom_13 (.addr(5'b00111), .data(rom_13_data));  // open: sel
  assign and_23_out = rom_13_data & zz;  // AND_Gate and_23, 20 bits wide
  ROM #(.addrWidth(5), .dataWidth(20)) rom_14 (.addr(5'b01010), .data(rom_14_data));  // open: sel
  assign and_24_out = rom_14_data & zz;  // AND_Gate and_24, 20 bits wide
  ROM #(.addrWidth(5), .dataWidth(20)) rom_15 (.addr(5'b01101), .data(rom_15_data));  // open: sel
  assign and_25_out = rom_15_data & zz;  // AND_Gate and_25, 20 bits wide
  ROM #(.addrWidth(5), .dataWidth(20)) rom_16 (.addr(5'b10000), .data(rom_16_data));  // open: sel
  assign and_26_out = rom_16_data & zz;  // AND_Gate and_26, 20 bits wide
  ROM #(.addrWidth(5), .dataWidth(20)) rom_17 (.addr(5'b10011), .data(rom_17_data));  // open: sel
  assign and_27_out = rom_17_data & zz;  // AND_Gate and_27, 20 bits wide
  ROM #(.addrWidth(5), .dataWidth(20)) rom_18 (.addr(5'b10110), .data(rom_18_data));  // open: sel
  assign and_28_out = rom_18_data & zz;  // AND_Gate and_28, 20 bits wide
  Multiplexer #(.width(9)) multiplexer_14 (.in0(aa), .in1(bb), .out(multiplexer_14_out), .sel(cc));  // open: en
  Multiplexer #(.width(9)) multiplexer_15 (.in0(xx), .in1(tempx), .out(multiplexer_15_out), .sel(cc));  // open: en
  Multiplexer #(.width(9)) multiplexer_16 (.in0(yy), .in1(tempy), .out(multiplexer_16_out), .sel(cc));  // open: en
  Multiplexer #(.width(9)) multiplexer_17 (
    .in0(multiplexer_15_out), .in1(startx), .out(multiplexer_17_out), .sel(in_1));  // open: en
  Multiplexer #(.width(9)) multiplexer_18 (
    .in0(multiplexer_16_out), .in1(starty), .out(multiplexer_18_out), .sel(in_1));  // open: en
  Multiplexer #(.width(20)) multiplexer_19 (
    .in0(rom_11_data), .in1(and_21_out), .out(out_6), .sel(and_29_out));  // open: en
  and and_29 (and_29_out, comparator_16_eq, temp_clk);
  Comparator #(.width(9)) comparator_16 (.a(xx), .b(9'h1), .eq(comparator_16_eq));  // open: gt, lt
  Multiplexer #(.width(20)) multiplexer_20 (
    .in0(rom_12_data), .in1(and_22_out), .out(out_9), .sel(and_30_out));  // open: en
  and and_30 (and_30_out, comparator_17_eq, temp_clk);
  Comparator #(.width(9)) comparator_17 (.a(xx), .b(9'h4), .eq(comparator_17_eq));  // open: gt, lt
  Multiplexer #(.width(20)) multiplexer_21 (
    .in0(rom_13_data), .in1(and_23_out), .out(out_12), .sel(and_31_out));  // open: en
  and and_31 (and_31_out, comparator_18_eq, temp_clk);
  Comparator #(.width(9)) comparator_18 (.a(xx), .b(9'h7), .eq(comparator_18_eq));  // open: gt, lt
  Multiplexer #(.width(20)) multiplexer_22 (
    .in0(rom_14_data), .in1(and_24_out), .out(out_15), .sel(and_32_out));  // open: en
  and and_32 (and_32_out, comparator_19_eq, temp_clk);
  Comparator #(.width(9)) comparator_19 (.a(xx), .b(9'ha), .eq(comparator_19_eq));  // open: gt, lt
  Multiplexer #(.width(20)) multiplexer_23 (
    .in0(rom_15_data), .in1(and_25_out), .out(out_18), .sel(and_33_out));  // open: en
  and and_33 (and_33_out, comparator_20_eq, temp_clk);
  Comparator #(.width(9)) comparator_20 (.a(xx), .b(9'hd), .eq(comparator_20_eq));  // open: gt, lt
  Multiplexer #(.width(20)) multiplexer_24 (
    .in0(rom_16_data), .in1(and_26_out), .out(out_21), .sel(and_34_out));  // open: en
  and and_34 (and_34_out, comparator_21_eq, temp_clk);
  Comparator #(.width(9)) comparator_21 (.a(xx), .b(9'h10), .eq(comparator_21_eq));  // open: gt, lt
  Multiplexer #(.width(20)) multiplexer_25 (
    .in0(rom_17_data), .in1(and_27_out), .out(out_24), .sel(and_35_out));  // open: en
  and and_35 (and_35_out, comparator_22_eq, temp_clk);
  Comparator #(.width(9)) comparator_22 (.a(xx), .b(9'h13), .eq(comparator_22_eq));  // open: gt, lt
  Multiplexer #(.width(20)) multiplexer_26 (
    .in0(rom_18_data), .in1(and_28_out), .out(out_27), .sel(and_36_out));  // open: en
  and and_36 (and_36_out, comparator_23_eq, temp_clk);
  Comparator #(.width(9)) comparator_23 (.a(xx), .b(9'h16), .eq(comparator_23_eq));  // open: gt, lt
  Multiplexer #(.width(9)) multiplexer_27 (
    .in0(multiplexer_14_out), .in1(9'h8), .out(multiplexer_27_out), .sel(in_1));  // open: en
  ROM #(.addrWidth(9), .dataWidth(1)) rom_19 (.addr(bb), .data(cc));  // open: sel
  Divider #(.width(9)) divider_1 (.a(bb), .b(9'h14), .out(tempx), .rem(tempy));  // open: upper
  Divider #(.width(9)) divider_2 (.a(9'h8), .b(9'h14), .out(startx), .rem(starty));  // open: upper
  Register #(.width(9)) register_3 (.D(multiplexer_17_out), .Q(xx), .clk(clk), .clr(undriven_3));  // open: en
  Register #(.width(9)) register_4 (.D(multiplexer_18_out), .Q(yy), .clk(clk), .clr(undriven_4));  // open: en
  Adder #(.width(4)) adder_3 (.a(ss), .b(4'b0001), .out(adder_3_out));  // open: cin, cout
  Register #(.width(9)) register_5 (.D(multiplexer_27_out), .Q(aa), .clk(clk), .clr(undriven_5));  // open: en
  Register #(.width(4)) register_6 (.D(adder_3_out), .Q(ss), .clk(clk), .clr(put));  // open: en
  ROM #(.addrWidth(5), .dataWidth(20)) rom_20 (.addr(5'b10100), .data(rom_20_data));  // open: sel
  assign and_37_out = rom_20_data & zz;  // AND_Gate and_37, 20 bits wide
  ROM #(.addrWidth(5), .dataWidth(20)) rom_21 (.addr(5'b10111), .data(rom_21_data));  // open: sel
  assign and_38_out = rom_21_data & zz;  // AND_Gate and_38, 20 bits wide
  Multiplexer #(.select(4)) multiplexer_28 (
    .in0(1'b0), .in1(1'b0), .in2(1'b0), .in3(1'b0), .in4(1'b0), .in5(1'b0), .in6(1'b0), .in7(1'b1),
    .in8(1'b1), .in9(1'b1), .in10(1'b1), .in11(1'b1), .in12(1'b1), .in13(1'b1), .in14(1'b1), .in15(1'b1),
    .out(temp_clk), .sel(ss));  // open: en
  ROM #(.addrWidth(5), .dataWidth(20)) rom_22 (.addr(5'b00010), .data(rom_22_data));  // open: sel
  assign and_39_out = rom_22_data & zz;  // AND_Gate and_39, 20 bits wide
  ROM #(.addrWidth(5), .dataWidth(20)) rom_23 (.addr(5'b00101), .data(rom_23_data));  // open: sel
  assign and_40_out = rom_23_data & zz;  // AND_Gate and_40, 20 bits wide
  ROM #(.addrWidth(5), .dataWidth(20)) rom_24 (.addr(5'b01000), .data(rom_24_data));  // open: sel
  assign and_41_out = rom_24_data & zz;  // AND_Gate and_41, 20 bits wide
  ROM #(.addrWidth(5), .dataWidth(20)) rom_25 (.addr(5'b01011), .data(rom_25_data));  // open: sel
  assign and_42_out = rom_25_data & zz;  // AND_Gate and_42, 20 bits wide
  ROM #(.addrWidth(5), .dataWidth(20)) rom_26 (.addr(5'b01110), .data(rom_26_data));  // open: sel
  assign and_43_out = rom_26_data & zz;  // AND_Gate and_43, 20 bits wide
  ROM #(.addrWidth(5), .dataWidth(20)) rom_27 (.addr(5'b10001), .data(rom_27_data));  // open: sel
  assign and_44_out = rom_27_data & zz;  // AND_Gate and_44, 20 bits wide
  Multiplexer #(.width(20)) multiplexer_29 (
    .in0(rom_22_data), .in1(and_39_out), .out(out_7), .sel(and_47_out));  // open: en
  Comparator #(.width(9)) comparator_24 (.a(xx), .b(9'h2), .eq(comparator_24_eq));  // open: gt, lt
  Multiplexer #(.width(20)) multiplexer_30 (
    .in0(rom_23_data), .in1(and_40_out), .out(out_10), .sel(and_48_out));  // open: en
  Comparator #(.width(9)) comparator_25 (.a(xx), .b(9'h5), .eq(comparator_25_eq));  // open: gt, lt
  Multiplexer #(.width(20)) multiplexer_31 (
    .in0(rom_24_data), .in1(and_41_out), .out(out_13), .sel(and_49_out));  // open: en
  Comparator #(.width(9)) comparator_26 (.a(xx), .b(9'h8), .eq(comparator_26_eq));  // open: gt, lt
  Multiplexer #(.width(20)) multiplexer_32 (
    .in0(rom_25_data), .in1(and_42_out), .out(out_16), .sel(and_50_out));  // open: en
  Comparator #(.width(9)) comparator_27 (.a(xx), .b(9'hb), .eq(comparator_27_eq));  // open: gt, lt
  Multiplexer #(.width(20)) multiplexer_33 (
    .in0(rom_26_data), .in1(and_43_out), .out(out_19), .sel(and_51_out));  // open: en
  Comparator #(.width(9)) comparator_28 (.a(xx), .b(9'he), .eq(comparator_28_eq));  // open: gt, lt
  Multiplexer #(.width(20)) multiplexer_34 (
    .in0(rom_27_data), .in1(and_44_out), .out(out_22), .sel(and_52_out));  // open: en
  Comparator #(.width(9)) comparator_29 (.a(xx), .b(9'h11), .eq(comparator_29_eq));  // open: gt, lt
  Multiplexer #(.width(20)) multiplexer_35 (
    .in0(rom_20_data), .in1(and_37_out), .out(out_25), .sel(and_45_out));  // open: en
  and and_45 (and_45_out, comparator_30_eq, temp_clk);
  Comparator #(.width(9)) comparator_30 (.a(xx), .b(9'h14), .eq(comparator_30_eq));  // open: gt, lt
  Multiplexer #(.width(20)) multiplexer_36 (
    .in0(rom_21_data), .in1(and_38_out), .out(out_28), .sel(and_46_out));  // open: en
  and and_46 (and_46_out, comparator_31_eq, temp_clk);
  Comparator #(.width(9)) comparator_31 (.a(xx), .b(9'h17), .eq(comparator_31_eq));  // open: gt, lt
  and and_47 (and_47_out, comparator_24_eq, temp_clk);
  and and_48 (and_48_out, comparator_25_eq, temp_clk);
  and and_49 (and_49_out, comparator_26_eq, temp_clk);
  and and_50 (and_50_out, comparator_27_eq, temp_clk);
  and and_51 (and_51_out, comparator_28_eq, temp_clk);
  and and_52 (and_52_out, comparator_29_eq, temp_clk);

  // Other names for the same wires on the sheet: ggg = out_30; keyboard_t[6:0] = in_3; reset = in_1;
  //   stage[2:0] = out_4; thisstage[2:0] = in_2

  // Notes on the sheet:
  //   contents of rom_1 (hex, n*v repeats v):
  //   800 5fed4 5509e 457d0 7d516 21452 7f7f6 1404 75dfe 1c810 77fbe 20902 7bbd6 10172 3bf3a 6e58e 42cfa
  //   5e982 33e 7ff92 420d8 6ed8e 28538 6fd6e 800
  //   contents of rom_2 (hex, n*v repeats v):
  //   800 5fed4 5509e 457d0 7d516 21452 7f7f6 1404 75dfe 1c810 77fbe 20902 7bbd6 10172 3bf3a 6e58e 42cfa
  //   5e982 33e 7ff92 420d8 6ed8e 28538 6fd6e 800
  //   contents of rom_3 (hex, n*v repeats v):
  //   800 5fed4 5509e 457d0 7d516 21452 7f7f6 1404 75dfe 1c810 77fbe 20902 7bbd6 10172 3bf3a 6e58e 42cfa
  //   5e982 33e 7ff92 420d8 6ed8e 28538 6fd6e 800
  //   contents of rom_4 (hex, n*v repeats v):
  //   800 5fed4 5509e 457d0 7d516 21452 7f7f6 1404 75dfe 1c810 77fbe 20902 7bbd6 10172 3bf3a 6e58e 42cfa
  //   5e982 33e 7ff92 420d8 6ed8e 28538 6fd6e 800
  //   contents of rom_5 (hex, n*v repeats v):
  //   800 5fed4 5509e 457d0 7d516 21452 7f7f6 1404 75dfe 1c810 77fbe 20902 7bbd6 10172 3bf3a 6e58e 42cfa
  //   5e982 33e 7ff92 420d8 6ed8e 28538 6fd6e 800
  //   contents of rom_6 (hex, n*v repeats v):
  //   800 5fed4 5509e 457d0 7d516 21452 7f7f6 1404 75dfe 1c810 77fbe 20902 7bbd6 10172 3bf3a 6e58e 42cfa
  //   5e982 33e 7ff92 420d8 6ed8e 28538 6fd6e 800
  //   contents of rom_7 (hex, n*v repeats v):
  //   800 5fed4 5509e 457d0 7d516 21452 7f7f6 1404 75dfe 1c810 77fbe 20902 7bbd6 10172 3bf3a 6e58e 42cfa
  //   5e982 33e 7ff92 420d8 6ed8e 28538 6fd6e 800
  //   contents of rom_8 (hex, n*v repeats v):
  //   800 5fed4 5509e 457d0 7d516 21452 7f7f6 1404 75dfe 1c810 77fbe 20902 7bbd6 10172 3bf3a 6e58e 42cfa
  //   5e982 33e 7ff92 420d8 6ed8e 28538 6fd6e 800
  //   contents of rom_9 (hex, n*v repeats v):
  //   800 5fed4 5509e 457d0 7d516 21452 7f7f6 1404 75dfe 1c810 77fbe 20902 7bbd6 10172 3bf3a 6e58e 42cfa
  //   5e982 33e 7ff92 420d8 6ed8e 28538 6fd6e 800
  //   contents of rom_10 (hex, n*v repeats v):
  //   80000 40000 20000 10000 8000 4000 2000 1000 800 400 200 100 80 40 20 10 8 4 2 1 4*0 800
  //   a
  //   w
  //   s
  //   d
  //   contents of rom_11 (hex, n*v repeats v):
  //   800 5fed4 5509e 457d0 7d516 21452 7f7f6 1404 75dfe 1c810 77fbe 20902 7bbd6 10172 3bf3a 6e58e 42cfa
  //   5e982 33e 7ff92 420d8 6ed8e 28538 6fd6e 800
  //   contents of rom_12 (hex, n*v repeats v):
  //   800 5fed4 5509e 457d0 7d516 21452 7f7f6 1404 75dfe 1c810 77fbe 20902 7bbd6 10172 3bf3a 6e58e 42cfa
  //   5e982 33e 7ff92 420d8 6ed8e 28538 6fd6e 800
  //   contents of rom_13 (hex, n*v repeats v):
  //   800 5fed4 5509e 457d0 7d516 21452 7f7f6 1404 75dfe 1c810 77fbe 20902 7bbd6 10172 3bf3a 6e58e 42cfa
  //   5e982 33e 7ff92 420d8 6ed8e 28538 6fd6e 800
  //   contents of rom_14 (hex, n*v repeats v):
  //   800 5fed4 5509e 457d0 7d516 21452 7f7f6 1404 75dfe 1c810 77fbe 20902 7bbd6 10172 3bf3a 6e58e 42cfa
  //   5e982 33e 7ff92 420d8 6ed8e 28538 6fd6e 800
  //   contents of rom_15 (hex, n*v repeats v):
  //   800 5fed4 5509e 457d0 7d516 21452 7f7f6 1404 75dfe 1c810 77fbe 20902 7bbd6 10172 3bf3a 6e58e 42cfa
  //   5e982 33e 7ff92 420d8 6ed8e 28538 6fd6e 800
  //   contents of rom_16 (hex, n*v repeats v):
  //   800 5fed4 5509e 457d0 7d516 21452 7f7f6 1404 75dfe 1c810 77fbe 20902 7bbd6 10172 3bf3a 6e58e 42cfa
  //   5e982 33e 7ff92 420d8 6ed8e 28538 6fd6e 800
  //   contents of rom_17 (hex, n*v repeats v):
  //   800 5fed4 5509e 457d0 7d516 21452 7f7f6 1404 75dfe 1c810 77fbe 20902 7bbd6 10172 3bf3a 6e58e 42cfa
  //   5e982 33e 7ff92 420d8 6ed8e 28538 6fd6e 800
  //   contents of rom_18 (hex, n*v repeats v):
  //   800 5fed4 5509e 457d0 7d516 21452 7f7f6 1404 75dfe 1c810 77fbe 20902 7bbd6 10172 3bf3a 6e58e 42cfa
  //   5e982 33e 7ff92 420d8 6ed8e 28538 6fd6e 800
  //   contents of rom_19 (hex, n*v repeats v):
  //   8*0 1 12*0 1 0 8*1 0 1 1 0 1 0 1 0 0 0 1 0 1 0 1 0 1 4*0 1 0 0 4*1 0 0 1 0 0 0 1 0 1 0 5*1 0 1 5*0
  //   5*1 0 1 0 1 0 1 0 0 0 1 0 1 1 0 0 0 1 4*0 1 0 1 0 0 0 1 0 1 0 0 1 0 0 7*1 0 7*1 0 1 1 8*0 1 0 1 7*0
  //   1 0 0 0 1 1 1 0 1 0 1 1 1 0 8*1 4*0 1 1 1 0 0 1 6*0 1 5*0 1 1 1 0 8*1 0 5*1 0 0 0 1 5*0 1 0 0 1 6*0
  //   1 0 0 4*1 0 1 1 1 0 4*1 0 1 0 1 1 4*0 1 7*0 1 0 1 1 1 0 0 1 0 0 0 1 1 1 0 6*1 0 0 1 1 1 0 1 0 0 1 1
  //   0 1 1 1 0 0 1 0 1 1 0 0 0 1 1 1 0 0 1 4*0 1 0 1 1 0 0 5*1 0 1 0 0 1 0 4*1 0 1 0 0 1 1 5*0 1 11*0 1 1
  //   0 0 5*1 0 0 12*1 0 0 1 0 0 1 0 0 1 4*0 1 5*0 1 1 0 1 1 4*0 1 1 0 1 1 1 0 1 1 0 1 1 0 0 0 1 1 1 0 0 0
  //   1 0 1 4*0 1 0 1 0 0 1 1 1 4*0 1 1 0 6*1 0 1 0 1 1 0 1 1 1 9*0 1
  //   contents of rom_20 (hex, n*v repeats v):
  //   800 5fed4 5509e 457d0 7d516 21452 7f7f6 1404 75dfe 1c810 77fbe 20902 7bbd6 10172 3bf3a 6e58e 42cfa
  //   5e982 33e 7ff92 420d8 6ed8e 28538 6fd6e 800
  //   contents of rom_21 (hex, n*v repeats v):
  //   800 5fed4 5509e 457d0 7d516 21452 7f7f6 1404 75dfe 1c810 77fbe 20902 7bbd6 10172 3bf3a 6e58e 42cfa
  //   5e982 33e 7ff92 420d8 6ed8e 28538 6fd6e 800
  //   contents of rom_22 (hex, n*v repeats v):
  //   800 5fed4 5509e 457d0 7d516 21452 7f7f6 1404 75dfe 1c810 77fbe 20902 7bbd6 10172 3bf3a 6e58e 42cfa
  //   5e982 33e 7ff92 420d8 6ed8e 28538 6fd6e 800
  //   contents of rom_23 (hex, n*v repeats v):
  //   800 5fed4 5509e 457d0 7d516 21452 7f7f6 1404 75dfe 1c810 77fbe 20902 7bbd6 10172 3bf3a 6e58e 42cfa
  //   5e982 33e 7ff92 420d8 6ed8e 28538 6fd6e 800
  //   contents of rom_24 (hex, n*v repeats v):
  //   800 5fed4 5509e 457d0 7d516 21452 7f7f6 1404 75dfe 1c810 77fbe 20902 7bbd6 10172 3bf3a 6e58e 42cfa
  //   5e982 33e 7ff92 420d8 6ed8e 28538 6fd6e 800
  //   contents of rom_25 (hex, n*v repeats v):
  //   800 5fed4 5509e 457d0 7d516 21452 7f7f6 1404 75dfe 1c810 77fbe 20902 7bbd6 10172 3bf3a 6e58e 42cfa
  //   5e982 33e 7ff92 420d8 6ed8e 28538 6fd6e 800
  //   contents of rom_26 (hex, n*v repeats v):
  //   800 5fed4 5509e 457d0 7d516 21452 7f7f6 1404 75dfe 1c810 77fbe 20902 7bbd6 10172 3bf3a 6e58e 42cfa
  //   5e982 33e 7ff92 420d8 6ed8e 28538 6fd6e 800
  //   contents of rom_27 (hex, n*v repeats v):
  //   800 5fed4 5509e 457d0 7d516 21452 7f7f6 1404 75dfe 1c810 77fbe 20902 7bbd6 10172 3bf3a 6e58e 42cfa
  //   5e982 33e 7ff92 420d8 6ed8e 28538 6fd6e 800
endmodule

module stage3 (
  input  in_1,
  input  [2:0] in_2,
  input  [6:0] in_3,
  output [2:0] out_4,
  output [19:0] out_5,
  output [19:0] out_6,
  output [19:0] out_7,
  output [19:0] out_8,
  output [19:0] out_9,
  output [19:0] out_10,
  output [19:0] out_11,
  output [19:0] out_12,
  output [19:0] out_13,
  output [19:0] out_14,
  output [19:0] out_15,
  output [19:0] out_16,
  output [19:0] out_17,
  output [19:0] out_18,
  output [19:0] out_19,
  output [19:0] out_20,
  output [19:0] out_21,
  output [19:0] out_22,
  output [19:0] out_23,
  output [19:0] out_24,
  output [19:0] out_25,
  output [19:0] out_26,
  output [19:0] out_27,
  output [19:0] out_28,
  output [19:0] out_29,
  output out_30
);

  wire a, and_10_out, and_11_out, and_12_out, and_13_out, and_14_out, and_15_out, and_16_out, and_17_out,
       and_18_out, and_29_out, and_30_out, and_31_out, and_32_out, and_33_out, and_34_out, and_35_out,
       and_36_out, and_45_out, and_46_out, and_47_out, and_48_out, and_49_out, and_50_out, and_51_out,
       and_52_out, cc, clk, comparator_2_eq, comparator_3_eq, comparator_4_eq, comparator_5_eq,
       comparator_6_eq, comparator_7_eq, comparator_8_eq, comparator_9_eq, comparator_10_eq,
       comparator_15_gt, comparator_16_eq, comparator_17_eq, comparator_18_eq, comparator_19_eq,
       comparator_20_eq, comparator_21_eq, comparator_22_eq, comparator_23_eq, comparator_24_eq,
       comparator_25_eq, comparator_26_eq, comparator_27_eq, comparator_28_eq, comparator_29_eq,
       comparator_30_eq, comparator_31_eq, d, multiplexer_11_out, not_1_out, not_3_out, put, s, temp_clk,
       undriven, undriven_2, undriven_3, undriven_4, undriven_5, w;
  wire [1:0] and_19_out;
  wire [2:0] multiplexer_10_out, multiplexer_12_out;
  wire [3:0] adder_3_out, ss;
  wire [6:0] keyboard;
  wire [8:0] aa, adder_1_out, adder_2_out, bb, multiplexer_14_out, multiplexer_15_out, multiplexer_16_out,
       multiplexer_25_out, multiplexer_26_out, multiplexer_27_out, startx, starty, subtractor_1_out,
       subtractor_2_out, tempx, tempy, xx, yy;
  wire [19:0] and_1_out, and_2_out, and_3_out, and_4_out, and_5_out, and_6_out, and_7_out, and_8_out,
       and_9_out, and_21_out, and_22_out, and_23_out, and_24_out, and_25_out, and_26_out, and_27_out,
       and_28_out, and_37_out, and_38_out, and_39_out, and_40_out, and_41_out, and_42_out, and_43_out,
       and_44_out, rom_1_data, rom_2_data, rom_3_data, rom_4_data, rom_5_data, rom_6_data, rom_7_data,
       rom_8_data, rom_9_data, rom_10_data, rom_11_data, rom_12_data, rom_13_data, rom_14_data, rom_15_data,
       rom_16_data, rom_17_data, rom_18_data, rom_20_data, rom_21_data, rom_22_data, rom_23_data,
       rom_24_data, rom_25_data, rom_26_data, rom_27_data, zz;

  Clock clock_1 (.out(clk));
  ROM #(.addrWidth(5), .dataWidth(20)) rom_1 (.addr({5{1'b0}}), .data(rom_1_data));  // open: sel
  assign and_1_out = rom_1_data & zz;  // AND_Gate and_1, 20 bits wide
  ROM #(.addrWidth(5), .dataWidth(20)) rom_2 (.addr(5'b00011), .data(rom_2_data));  // open: sel
  assign and_2_out = rom_2_data & zz;  // AND_Gate and_2, 20 bits wide
  ROM #(.addrWidth(5), .dataWidth(20)) rom_3 (.addr(5'b00110), .data(rom_3_data));  // open: sel
  assign and_3_out = rom_3_data & zz;  // AND_Gate and_3, 20 bits wide
  ROM #(.addrWidth(5), .dataWidth(20)) rom_4 (.addr(5'b01001), .data(rom_4_data));  // open: sel
  assign and_4_out = rom_4_data & zz;  // AND_Gate and_4, 20 bits wide
  ROM #(.addrWidth(5), .dataWidth(20)) rom_5 (.addr(5'b01100), .data(rom_5_data));  // open: sel
  assign and_5_out = rom_5_data & zz;  // AND_Gate and_5, 20 bits wide
  ROM #(.addrWidth(5), .dataWidth(20)) rom_6 (.addr(5'b01111), .data(rom_6_data));  // open: sel
  assign and_6_out = rom_6_data & zz;  // AND_Gate and_6, 20 bits wide
  ROM #(.addrWidth(5), .dataWidth(20)) rom_7 (.addr(5'b10010), .data(rom_7_data));  // open: sel
  assign and_7_out = rom_7_data & zz;  // AND_Gate and_7, 20 bits wide
  ROM #(.addrWidth(5), .dataWidth(20)) rom_8 (.addr(5'b10101), .data(rom_8_data));  // open: sel
  assign and_8_out = rom_8_data & zz;  // AND_Gate and_8, 20 bits wide
  ROM #(.addrWidth(5), .dataWidth(20)) rom_9 (.addr(5'b11000), .data(rom_9_data));  // open: sel
  assign and_9_out = rom_9_data & zz;  // AND_Gate and_9, 20 bits wide
  ROM #(.addrWidth(9), .dataWidth(20)) rom_10 (.addr(yy), .data(rom_10_data));  // open: sel
  Comparator #(.width(9)) comparator_1 (.a(aa), .b(9'h1e8), .eq(and_19_out[1]));  // open: gt, lt
  not not_1 (not_1_out, cc);
  assign zz = ~rom_10_data;  // NOT_Gate not_2, 20 bits wide
  Multiplexer #(.width(20)) multiplexer_1 (
    .in0(rom_1_data), .in1(and_1_out), .out(out_5), .sel(and_10_out));  // open: en
  and and_10 (and_10_out, comparator_2_eq, temp_clk);
  Comparator #(.width(9)) comparator_2 (.a(xx), .b({9{1'b0}}), .eq(comparator_2_eq));  // open: gt, lt
  Multiplexer #(.width(20)) multiplexer_2 (
    .in0(rom_2_data), .in1(and_2_out), .out(out_8), .sel(and_11_out));  // open: en
  and and_11 (and_11_out, comparator_3_eq, temp_clk);
  Comparator #(.width(9)) comparator_3 (.a(xx), .b(9'h3), .eq(comparator_3_eq));  // open: gt, lt
  Multiplexer #(.width(20)) multiplexer_3 (
    .in0(rom_3_data), .in1(and_3_out), .out(out_11), .sel(and_12_out));  // open: en
  and and_12 (and_12_out, comparator_4_eq, temp_clk);
  Comparator #(.width(9)) comparator_4 (.a(xx), .b(9'h6), .eq(comparator_4_eq));  // open: gt, lt
  Multiplexer #(.width(20)) multiplexer_4 (
    .in0(rom_4_data), .in1(and_4_out), .out(out_14), .sel(and_13_out));  // open: en
  and and_13 (and_13_out, comparator_5_eq, temp_clk);
  Comparator #(.width(9)) comparator_5 (.a(xx), .b(9'h9), .eq(comparator_5_eq));  // open: gt, lt
  Multiplexer #(.width(20)) multiplexer_5 (
    .in0(rom_5_data), .in1(and_5_out), .out(out_17), .sel(and_14_out));  // open: en
  and and_14 (and_14_out, comparator_6_eq, temp_clk);
  Comparator #(.width(9)) comparator_6 (.a(xx), .b(9'hc), .eq(comparator_6_eq));  // open: gt, lt
  Multiplexer #(.width(20)) multiplexer_6 (
    .in0(rom_6_data), .in1(and_6_out), .out(out_20), .sel(and_15_out));  // open: en
  and and_15 (and_15_out, comparator_7_eq, temp_clk);
  Comparator #(.width(9)) comparator_7 (.a(xx), .b(9'hf), .eq(comparator_7_eq));  // open: gt, lt
  Multiplexer #(.width(20)) multiplexer_7 (
    .in0(rom_7_data), .in1(and_7_out), .out(out_23), .sel(and_16_out));  // open: en
  and and_16 (and_16_out, comparator_8_eq, temp_clk);
  Comparator #(.width(9)) comparator_8 (.a(xx), .b(9'h12), .eq(comparator_8_eq));  // open: gt, lt
  Multiplexer #(.width(20)) multiplexer_8 (
    .in0(rom_8_data), .in1(and_8_out), .out(out_26), .sel(and_17_out));  // open: en
  and and_17 (and_17_out, comparator_9_eq, temp_clk);
  Comparator #(.width(9)) comparator_9 (.a(xx), .b(9'h15), .eq(comparator_9_eq));  // open: gt, lt
  Multiplexer #(.width(20)) multiplexer_9 (
    .in0(rom_9_data), .in1(and_9_out), .out(out_29), .sel(and_18_out));  // open: en
  and and_18 (and_18_out, comparator_10_eq, temp_clk);
  Comparator #(.width(9)) comparator_10 (.a(xx), .b(9'h18), .eq(comparator_10_eq));  // open: gt, lt
  Comparator #(.width(7)) comparator_11 (.a(keyboard), .b(7'b1100001), .eq(a));  // open: gt, lt
  Comparator #(.width(7)) comparator_12 (.a(keyboard), .b(7'b1110111), .eq(w));  // open: gt, lt
  Comparator #(.width(7)) comparator_13 (.a(keyboard), .b(7'b1110011), .eq(s));  // open: gt, lt
  Comparator #(.width(7)) comparator_14 (.a(keyboard), .b(7'b1100100), .eq(d));  // open: gt, lt
  Multiplexer #(.select(2), .width(3)) multiplexer_10 (
    .in0(out_4), .in1(3'b100), .in2(3'b011), .in3(out_4), .out(multiplexer_10_out), .sel(and_19_out));  // open: en
  and and_19 (and_19_out[0], not_3_out, comparator_15_gt);
  not not_3 (not_3_out, cc);
  Multiplexer multiplexer_11 (.in0(1'b0), .in1(1'b1), .out(multiplexer_11_out), .sel(not_1_out));  // open: en
  Subtractor #(.width(9)) subtractor_1 (.a(aa), .b(9'h1), .out(subtractor_1_out));  // open: bin, bout
  Subtractor #(.width(9)) subtractor_2 (.a(aa), .b(9'h14), .out(subtractor_2_out));  // open: bin, bout
  Adder #(.width(9)) adder_1 (.a(aa), .b(9'h14), .out(adder_1_out));  // open: cin, cout
  Adder #(.width(9)) adder_2 (.a(aa), .b(9'h1), .out(adder_2_out));  // open: cin, cout
  Multiplexer #(.width(3)) multiplexer_12 (
    .in0(multiplexer_10_out), .in1(in_2), .out(multiplexer_12_out), .sel(in_1));  // open: en
  Comparator #(.width(9)) comparator_15 (.a(aa), .b(9'h8), .gt(comparator_15_gt));  // open: eq, lt
  Register #(.width(1)) register_1 (.D(multiplexer_11_out), .Q(out_30), .clk(clk), .clr(undriven));  // open: en
  TTY tty_1 (.data(in_3), .clk(clk));  // open: we, clr
  Register #(.width(3)) register_2 (.D(multiplexer_12_out), .Q(out_4), .clk(clk), .clr(undriven_2));  // open: en
  and and_20 (put, d, s, w, a);
  Multiplexer #(.select(4), .width(9)) multiplexer_13 (
    .in0(aa), .in1(subtractor_1_out), .in2(subtractor_2_out), .in3(aa), .in4(adder_1_out), .in5(aa),
    .in6(aa), .in7(aa), .in8(adder_2_out), .in9(aa), .in10(aa), .in11(aa), .in12(aa), .in13(aa), .in14(aa),
    .in15(aa), .out(bb), .sel({d, s, w, a}));  // open: en
  ROM #(.addrWidth(5), .dataWidth(20)) rom_11 (.addr(5'b00001), .data(rom_11_data));  // open: sel
  assign and_21_out = rom_11_data & zz;  // AND_Gate and_21, 20 bits wide
  ROM #(.addrWidth(5), .dataWidth(20)) rom_12 (.addr(5'b00100), .data(rom_12_data));  // open: sel
  assign and_22_out = rom_12_data & zz;  // AND_Gate and_22, 20 bits wide
  ROM #(.addrWidth(5), .dataWidth(20)) rom_13 (.addr(5'b00111), .data(rom_13_data));  // open: sel
  assign and_23_out = rom_13_data & zz;  // AND_Gate and_23, 20 bits wide
  ROM #(.addrWidth(5), .dataWidth(20)) rom_14 (.addr(5'b01010), .data(rom_14_data));  // open: sel
  assign and_24_out = rom_14_data & zz;  // AND_Gate and_24, 20 bits wide
  ROM #(.addrWidth(5), .dataWidth(20)) rom_15 (.addr(5'b01101), .data(rom_15_data));  // open: sel
  assign and_25_out = rom_15_data & zz;  // AND_Gate and_25, 20 bits wide
  ROM #(.addrWidth(5), .dataWidth(20)) rom_16 (.addr(5'b10000), .data(rom_16_data));  // open: sel
  assign and_26_out = rom_16_data & zz;  // AND_Gate and_26, 20 bits wide
  ROM #(.addrWidth(5), .dataWidth(20)) rom_17 (.addr(5'b10011), .data(rom_17_data));  // open: sel
  assign and_27_out = rom_17_data & zz;  // AND_Gate and_27, 20 bits wide
  ROM #(.addrWidth(5), .dataWidth(20)) rom_18 (.addr(5'b10110), .data(rom_18_data));  // open: sel
  assign and_28_out = rom_18_data & zz;  // AND_Gate and_28, 20 bits wide
  Multiplexer #(.width(9)) multiplexer_14 (.in0(xx), .in1(tempx), .out(multiplexer_14_out), .sel(cc));  // open: en
  Multiplexer #(.width(9)) multiplexer_15 (.in0(yy), .in1(tempy), .out(multiplexer_15_out), .sel(cc));  // open: en
  Multiplexer #(.width(9)) multiplexer_16 (.in0(aa), .in1(bb), .out(multiplexer_16_out), .sel(cc));  // open: en
  Multiplexer #(.width(20)) multiplexer_17 (
    .in0(rom_11_data), .in1(and_21_out), .out(out_6), .sel(and_29_out));  // open: en
  and and_29 (and_29_out, comparator_16_eq, temp_clk);
  Comparator #(.width(9)) comparator_16 (.a(xx), .b(9'h1), .eq(comparator_16_eq));  // open: gt, lt
  Multiplexer #(.width(20)) multiplexer_18 (
    .in0(rom_12_data), .in1(and_22_out), .out(out_9), .sel(and_30_out));  // open: en
  and and_30 (and_30_out, comparator_17_eq, temp_clk);
  Comparator #(.width(9)) comparator_17 (.a(xx), .b(9'h4), .eq(comparator_17_eq));  // open: gt, lt
  Multiplexer #(.width(20)) multiplexer_19 (
    .in0(rom_13_data), .in1(and_23_out), .out(out_12), .sel(and_31_out));  // open: en
  and and_31 (and_31_out, comparator_18_eq, temp_clk);
  Comparator #(.width(9)) comparator_18 (.a(xx), .b(9'h7), .eq(comparator_18_eq));  // open: gt, lt
  Multiplexer #(.width(20)) multiplexer_20 (
    .in0(rom_14_data), .in1(and_24_out), .out(out_15), .sel(and_32_out));  // open: en
  and and_32 (and_32_out, comparator_19_eq, temp_clk);
  Comparator #(.width(9)) comparator_19 (.a(xx), .b(9'ha), .eq(comparator_19_eq));  // open: gt, lt
  Multiplexer #(.width(20)) multiplexer_21 (
    .in0(rom_15_data), .in1(and_25_out), .out(out_18), .sel(and_33_out));  // open: en
  and and_33 (and_33_out, comparator_20_eq, temp_clk);
  Comparator #(.width(9)) comparator_20 (.a(xx), .b(9'hd), .eq(comparator_20_eq));  // open: gt, lt
  Multiplexer #(.width(20)) multiplexer_22 (
    .in0(rom_16_data), .in1(and_26_out), .out(out_21), .sel(and_34_out));  // open: en
  and and_34 (and_34_out, comparator_21_eq, temp_clk);
  Comparator #(.width(9)) comparator_21 (.a(xx), .b(9'h10), .eq(comparator_21_eq));  // open: gt, lt
  Multiplexer #(.width(20)) multiplexer_23 (
    .in0(rom_17_data), .in1(and_27_out), .out(out_24), .sel(and_35_out));  // open: en
  and and_35 (and_35_out, comparator_22_eq, temp_clk);
  Comparator #(.width(9)) comparator_22 (.a(xx), .b(9'h13), .eq(comparator_22_eq));  // open: gt, lt
  Multiplexer #(.width(20)) multiplexer_24 (
    .in0(rom_18_data), .in1(and_28_out), .out(out_27), .sel(and_36_out));  // open: en
  and and_36 (and_36_out, comparator_23_eq, temp_clk);
  Comparator #(.width(9)) comparator_23 (.a(xx), .b(9'h16), .eq(comparator_23_eq));  // open: gt, lt
  Multiplexer #(.width(9)) multiplexer_25 (
    .in0(multiplexer_16_out), .in1(9'h8), .out(multiplexer_25_out), .sel(in_1));  // open: en
  Divider #(.width(9)) divider_1 (.a(bb), .b(9'h14), .out(tempx), .rem(tempy));  // open: upper
  Divider #(.width(9)) divider_2 (.a(9'h8), .b(9'h14), .out(startx), .rem(starty));  // open: upper
  Multiplexer #(.width(9)) multiplexer_26 (
    .in0(multiplexer_14_out), .in1(startx), .out(multiplexer_26_out), .sel(in_1));  // open: en
  Multiplexer #(.width(9)) multiplexer_27 (
    .in0(multiplexer_15_out), .in1(starty), .out(multiplexer_27_out), .sel(in_1));  // open: en
  Adder #(.width(4)) adder_3 (.a(ss), .b(4'b0001), .out(adder_3_out));  // open: cin, cout
  ROM #(.addrWidth(9), .dataWidth(1)) rom_19 (.addr(bb), .data(cc));  // open: sel
  Register #(.width(9)) register_3 (.D(multiplexer_26_out), .Q(xx), .clk(clk), .clr(undriven_3));  // open: en
  Register #(.width(9)) register_4 (.D(multiplexer_27_out), .Q(yy), .clk(clk), .clr(undriven_4));  // open: en
  Register #(.width(9)) register_5 (.D(multiplexer_25_out), .Q(aa), .clk(clk), .clr(undriven_5));  // open: en
  Register #(.width(4)) register_6 (.D(adder_3_out), .Q(ss), .clk(clk), .clr(put));  // open: en
  Multiplexer #(.select(4)) multiplexer_28 (
    .in0(1'b0), .in1(1'b0), .in2(1'b0), .in3(1'b0), .in4(1'b0), .in5(1'b0), .in6(1'b0), .in7(1'b1),
    .in8(1'b1), .in9(1'b1), .in10(1'b1), .in11(1'b1), .in12(1'b1), .in13(1'b1), .in14(1'b1), .in15(1'b1),
    .out(temp_clk), .sel(ss));  // open: en
  ROM #(.addrWidth(5), .dataWidth(20)) rom_20 (.addr(5'b00010), .data(rom_20_data));  // open: sel
  assign and_37_out = rom_20_data & zz;  // AND_Gate and_37, 20 bits wide
  ROM #(.addrWidth(5), .dataWidth(20)) rom_21 (.addr(5'b00101), .data(rom_21_data));  // open: sel
  assign and_38_out = rom_21_data & zz;  // AND_Gate and_38, 20 bits wide
  ROM #(.addrWidth(5), .dataWidth(20)) rom_22 (.addr(5'b01000), .data(rom_22_data));  // open: sel
  assign and_39_out = rom_22_data & zz;  // AND_Gate and_39, 20 bits wide
  ROM #(.addrWidth(5), .dataWidth(20)) rom_23 (.addr(5'b01011), .data(rom_23_data));  // open: sel
  assign and_40_out = rom_23_data & zz;  // AND_Gate and_40, 20 bits wide
  ROM #(.addrWidth(5), .dataWidth(20)) rom_24 (.addr(5'b01110), .data(rom_24_data));  // open: sel
  assign and_41_out = rom_24_data & zz;  // AND_Gate and_41, 20 bits wide
  ROM #(.addrWidth(5), .dataWidth(20)) rom_25 (.addr(5'b10001), .data(rom_25_data));  // open: sel
  assign and_42_out = rom_25_data & zz;  // AND_Gate and_42, 20 bits wide
  ROM #(.addrWidth(5), .dataWidth(20)) rom_26 (.addr(5'b10100), .data(rom_26_data));  // open: sel
  assign and_43_out = rom_26_data & zz;  // AND_Gate and_43, 20 bits wide
  ROM #(.addrWidth(5), .dataWidth(20)) rom_27 (.addr(5'b10111), .data(rom_27_data));  // open: sel
  assign and_44_out = rom_27_data & zz;  // AND_Gate and_44, 20 bits wide
  Comparator #(.width(9)) comparator_24 (.a(xx), .b(9'h2), .eq(comparator_24_eq));  // open: gt, lt
  Comparator #(.width(9)) comparator_25 (.a(xx), .b(9'h5), .eq(comparator_25_eq));  // open: gt, lt
  Comparator #(.width(9)) comparator_26 (.a(xx), .b(9'h8), .eq(comparator_26_eq));  // open: gt, lt
  Comparator #(.width(9)) comparator_27 (.a(xx), .b(9'hb), .eq(comparator_27_eq));  // open: gt, lt
  Comparator #(.width(9)) comparator_28 (.a(xx), .b(9'he), .eq(comparator_28_eq));  // open: gt, lt
  Comparator #(.width(9)) comparator_29 (.a(xx), .b(9'h11), .eq(comparator_29_eq));  // open: gt, lt
  Comparator #(.width(9)) comparator_30 (.a(xx), .b(9'h14), .eq(comparator_30_eq));  // open: gt, lt
  Comparator #(.width(9)) comparator_31 (.a(xx), .b(9'h17), .eq(comparator_31_eq));  // open: gt, lt
  Multiplexer #(.width(20)) multiplexer_29 (
    .in0(rom_20_data), .in1(and_37_out), .out(out_7), .sel(and_45_out));  // open: en
  and and_45 (and_45_out, comparator_24_eq, temp_clk);
  Multiplexer #(.width(20)) multiplexer_30 (
    .in0(rom_21_data), .in1(and_38_out), .out(out_10), .sel(and_46_out));  // open: en
  and and_46 (and_46_out, comparator_25_eq, temp_clk);
  Multiplexer #(.width(20)) multiplexer_31 (
    .in0(rom_22_data), .in1(and_39_out), .out(out_13), .sel(and_47_out));  // open: en
  and and_47 (and_47_out, comparator_26_eq, temp_clk);
  Multiplexer #(.width(20)) multiplexer_32 (
    .in0(rom_23_data), .in1(and_40_out), .out(out_16), .sel(and_48_out));  // open: en
  and and_48 (and_48_out, comparator_27_eq, temp_clk);
  Multiplexer #(.width(20)) multiplexer_33 (
    .in0(rom_24_data), .in1(and_41_out), .out(out_19), .sel(and_49_out));  // open: en
  and and_49 (and_49_out, comparator_28_eq, temp_clk);
  Multiplexer #(.width(20)) multiplexer_34 (
    .in0(rom_25_data), .in1(and_42_out), .out(out_22), .sel(and_50_out));  // open: en
  and and_50 (and_50_out, comparator_29_eq, temp_clk);
  Multiplexer #(.width(20)) multiplexer_35 (
    .in0(rom_26_data), .in1(and_43_out), .out(out_25), .sel(and_51_out));  // open: en
  and and_51 (and_51_out, comparator_30_eq, temp_clk);
  Multiplexer #(.width(20)) multiplexer_36 (
    .in0(rom_27_data), .in1(and_44_out), .out(out_28), .sel(and_52_out));  // open: en
  and and_52 (and_52_out, comparator_31_eq, temp_clk);

  // Other names for the same wires on the sheet: ggg = out_30; keyboard_t[6:0] = in_3; reset = in_1;
  //   stage[2:0] = out_4; thisstage[2:0] = in_2

  // Notes on the sheet:
  //   contents of rom_1 (hex, n*v repeats v):
  //   800 6eefc 3ba86 3b0 7b916 48df2 6e89e 22ec2 7a8fa 4aba0 5bf2e 107a 7d7c8 4101e 7fff2 849a 7ddc2
  //   4049e 771f0 5d724 5147c 571c6 4512 7fdf6 800
  //   contents of rom_2 (hex, n*v repeats v):
  //   800 6eefc 3ba86 3b0 7b916 48df2 6e89e 22ec2 7a8fa 4aba0 5bf2e 107a 7d7c8 4101e 7fff2 849a 7ddc2
  //   4049e 771f0 5d724 5147c 571c6 4512 7fdf6 800
  //   contents of rom_3 (hex, n*v repeats v):
  //   800 6eefc 3ba86 3b0 7b916 48df2 6e89e 22ec2 7a8fa 4aba0 5bf2e 107a 7d7c8 4101e 7fff2 849a 7ddc2
  //   4049e 771f0 5d724 5147c 571c6 4512 7fdf6 800
  //   contents of rom_4 (hex, n*v repeats v):
  //   800 6eefc 3ba86 3b0 7b916 48df2 6e89e 22ec2 7a8fa 4aba0 5bf2e 107a 7d7c8 4101e 7fff2 849a 7ddc2
  //   4049e 771f0 5d724 5147c 571c6 4512 7fdf6 800
  //   contents of rom_5 (hex, n*v repeats v):
  //   800 6eefc 3ba86 3b0 7b916 48df2 6e89e 22ec2 7a8fa 4aba0 5bf2e 107a 7d7c8 4101e 7fff2 849a 7ddc2
  //   4049e 771f0 5d724 5147c 571c6 4512 7fdf6 800
  //   contents of rom_6 (hex, n*v repeats v):
  //   800 6eefc 3ba86 3b0 7b916 48df2 6e89e 22ec2 7a8fa 4aba0 5bf2e 107a 7d7c8 4101e 7fff2 849a 7ddc2
  //   4049e 771f0 5d724 5147c 571c6 4512 7fdf6 800
  //   contents of rom_7 (hex, n*v repeats v):
  //   800 6eefc 3ba86 3b0 7b916 48df2 6e89e 22ec2 7a8fa 4aba0 5bf2e 107a 7d7c8 4101e 7fff2 849a 7ddc2
  //   4049e 771f0 5d724 5147c 571c6 4512 7fdf6 800
  //   contents of rom_8 (hex, n*v repeats v):
  //   800 6eefc 3ba86 3b0 7b916 48df2 6e89e 22ec2 7a8fa 4aba0 5bf2e 107a 7d7c8 4101e 7fff2 849a 7ddc2
  //   4049e 771f0 5d724 5147c 571c6 4512 7fdf6 800
  //   contents of rom_9 (hex, n*v repeats v):
  //   800 6eefc 3ba86 3b0 7b916 48df2 6e89e 22ec2 7a8fa 4aba0 5bf2e 107a 7d7c8 4101e 7fff2 849a 7ddc2
  //   4049e 771f0 5d724 5147c 571c6 4512 7fdf6 800
  //   contents of rom_10 (hex, n*v repeats v):
  //   80000 40000 20000 10000 8000 4000 2000 1000 800 400 200 100 80 40 20 10 8 4 2 1 4*0 800
  //   a
  //   w
  //   s
  //   d
  //   contents of rom_11 (hex, n*v repeats v):
  //   800 6eefc 3ba86 3b0 7b916 48df2 6e89e 22ec2 7a8fa 4aba0 5bf2e 107a 7d7c8 4101e 7fff2 849a 7ddc2
  //   4049e 771f0 5d724 5147c 571c6 4512 7fdf6 800
  //   contents of rom_12 (hex, n*v repeats v):
  //   800 6eefc 3ba86 3b0 7b916 48df2 6e89e 22ec2 7a8fa 4aba0 5bf2e 107a 7d7c8 4101e 7fff2 849a 7ddc2
  //   4049e 771f0 5d724 5147c 571c6 4512 7fdf6 800
  //   contents of rom_13 (hex, n*v repeats v):
  //   800 6eefc 3ba86 3b0 7b916 48df2 6e89e 22ec2 7a8fa 4aba0 5bf2e 107a 7d7c8 4101e 7fff2 849a 7ddc2
  //   4049e 771f0 5d724 5147c 571c6 4512 7fdf6 800
  //   contents of rom_14 (hex, n*v repeats v):
  //   800 6eefc 3ba86 3b0 7b916 48df2 6e89e 22ec2 7a8fa 4aba0 5bf2e 107a 7d7c8 4101e 7fff2 849a 7ddc2
  //   4049e 771f0 5d724 5147c 571c6 4512 7fdf6 800
  //   contents of rom_15 (hex, n*v repeats v):
  //   800 6eefc 3ba86 3b0 7b916 48df2 6e89e 22ec2 7a8fa 4aba0 5bf2e 107a 7d7c8 4101e 7fff2 849a 7ddc2
  //   4049e 771f0 5d724 5147c 571c6 4512 7fdf6 800
  //   contents of rom_16 (hex, n*v repeats v):
  //   800 6eefc 3ba86 3b0 7b916 48df2 6e89e 22ec2 7a8fa 4aba0 5bf2e 107a 7d7c8 4101e 7fff2 849a 7ddc2
  //   4049e 771f0 5d724 5147c 571c6 4512 7fdf6 800
  //   contents of rom_17 (hex, n*v repeats v):
  //   800 6eefc 3ba86 3b0 7b916 48df2 6e89e 22ec2 7a8fa 4aba0 5bf2e 107a 7d7c8 4101e 7fff2 849a 7ddc2
  //   4049e 771f0 5d724 5147c 571c6 4512 7fdf6 800
  //   contents of rom_18 (hex, n*v repeats v):
  //   800 6eefc 3ba86 3b0 7b916 48df2 6e89e 22ec2 7a8fa 4aba0 5bf2e 107a 7d7c8 4101e 7fff2 849a 7ddc2
  //   4049e 771f0 5d724 5147c 571c6 4512 7fdf6 800
  //   contents of rom_19 (hex, n*v repeats v):
  //   8*0 1 12*0 1 1 0 1 1 1 0 1 1 1 0 6*1 4*0 1 1 1 0 1 1 1 0 1 0 1 4*0 1 1 11*0 1 1 1 0 1 1 5*0 4*1 0 1
  //   1 1 0 0 1 0 0 0 1 0 1 1 0 0 1 0 0 1 0 0 0 1 1 0 5*1 0 0 1 0 0 1 1 0 1 1 1 0 1 0 0 0 1 0 0 4*1 0 0 0
  //   1 0 0 0 1 0 1 1 1 0 1 1 4*0 1 0 0 4*1 0 1 0 1 0 0 0 5*1 0 1 0 0 1 0 0 1 0 1 0 1 0 1 1 1 0 1 6*0 1 0
  //   1 1 0 6*1 0 0 1 0 1 1 1 8*0 1 5*0 4*1 0 1 0 0 5*1 0 1 0 5*1 0 0 1 4*0 1 5*0 1 7*0 4*1 0 0 15*1 0 0 1
  //   5*0 1 4*0 1 0 0 1 0 0 1 1 0 1 0 0 5*1 0 1 1 1 0 1 1 1 4*0 1 0 0 1 7*0 1 0 0 1 0 0 4*1 0 0 1 1 1 0 1
  //   1 1 0 0 0 5*1 5*0 1 0 1 1 1 0 1 0 1 1 1 0 0 1 0 0 1 0 0 0 1 0 1 0 0 0 1 0 1 0 0 0 5*1 0 0 0 1 0 1 0
  //   1 1 1 0 0 0 1 1 1 0 0 0 1 1 6*0 1 0 0 0 1 0 1 0 0 0 1 0 0 1 0 0 9*1 0 5*1 0 1 1 9*0 1
  //   contents of rom_20 (hex, n*v repeats v):
  //   800 6eefc 3ba86 3b0 7b916 48df2 6e89e 22ec2 7a8fa 4aba0 5bf2e 107a 7d7c8 4101e 7fff2 849a 7ddc2
  //   4049e 771f0 5d724 5147c 571c6 4512 7fdf6 800
  //   contents of rom_21 (hex, n*v repeats v):
  //   800 6eefc 3ba86 3b0 7b916 48df2 6e89e 22ec2 7a8fa 4aba0 5bf2e 107a 7d7c8 4101e 7fff2 849a 7ddc2
  //   4049e 771f0 5d724 5147c 571c6 4512 7fdf6 800
  //   contents of rom_22 (hex, n*v repeats v):
  //   800 6eefc 3ba86 3b0 7b916 48df2 6e89e 22ec2 7a8fa 4aba0 5bf2e 107a 7d7c8 4101e 7fff2 849a 7ddc2
  //   4049e 771f0 5d724 5147c 571c6 4512 7fdf6 800
  //   contents of rom_23 (hex, n*v repeats v):
  //   800 6eefc 3ba86 3b0 7b916 48df2 6e89e 22ec2 7a8fa 4aba0 5bf2e 107a 7d7c8 4101e 7fff2 849a 7ddc2
  //   4049e 771f0 5d724 5147c 571c6 4512 7fdf6 800
  //   contents of rom_24 (hex, n*v repeats v):
  //   800 6eefc 3ba86 3b0 7b916 48df2 6e89e 22ec2 7a8fa 4aba0 5bf2e 107a 7d7c8 4101e 7fff2 849a 7ddc2
  //   4049e 771f0 5d724 5147c 571c6 4512 7fdf6 800
  //   contents of rom_25 (hex, n*v repeats v):
  //   800 6eefc 3ba86 3b0 7b916 48df2 6e89e 22ec2 7a8fa 4aba0 5bf2e 107a 7d7c8 4101e 7fff2 849a 7ddc2
  //   4049e 771f0 5d724 5147c 571c6 4512 7fdf6 800
  //   contents of rom_26 (hex, n*v repeats v):
  //   800 6eefc 3ba86 3b0 7b916 48df2 6e89e 22ec2 7a8fa 4aba0 5bf2e 107a 7d7c8 4101e 7fff2 849a 7ddc2
  //   4049e 771f0 5d724 5147c 571c6 4512 7fdf6 800
  //   contents of rom_27 (hex, n*v repeats v):
  //   800 6eefc 3ba86 3b0 7b916 48df2 6e89e 22ec2 7a8fa 4aba0 5bf2e 107a 7d7c8 4101e 7fff2 849a 7ddc2
  //   4049e 771f0 5d724 5147c 571c6 4512 7fdf6 800
endmodule

module victory (
  input  [2:0] in_1,
  output [2:0] out_2,
  output [19:0] out_3,
  output [19:0] out_4,
  output [19:0] out_5,
  output [19:0] out_6,
  output [19:0] out_7,
  output [19:0] out_8,
  output [19:0] out_9,
  output [19:0] out_10,
  output [19:0] out_11,
  output [19:0] out_12,
  output [19:0] out_13,
  output [19:0] out_14,
  output [19:0] out_15,
  output [19:0] out_16,
  output [19:0] out_17,
  output [19:0] out_18,
  output [19:0] out_19,
  output [19:0] out_20,
  output [19:0] out_21,
  output [19:0] out_22,
  output [19:0] out_23,
  output [19:0] out_24,
  output [19:0] out_25,
  output [19:0] out_26,
  output [19:0] out_27
);


  assign out_2 = 3'b011;
  assign out_3 = 20'hc367c;
  assign out_4 = 20'hc367c;
  assign out_5 = 20'h66660;
  assign out_6 = 20'h66660;
  assign out_7 = 20'h66660;
  assign out_8 = 20'h3c67c;
  assign out_9 = 20'h3c67c;
  assign out_10 = {20{1'b0}};
  assign out_11 = 20'hfdf8;
  assign out_12 = 20'hfdf8;
  assign out_13 = 20'h3198;
  assign out_14 = 20'h3198;
  assign out_15 = 20'h3198;
  assign out_16 = 20'h3198;
  assign out_17 = 20'h3198;
  assign out_18 = 20'h31f8;
  assign out_19 = {20{1'b0}};
  assign out_20 = 20'hf8c3;
  assign out_21 = 20'hc466;
  assign out_22 = 20'hcc24;
  assign out_23 = 20'hcc3c;
  assign out_24 = 20'hf818;
  assign out_25 = 20'hcc18;
  assign out_26 = 20'hc418;
  assign out_27 = 20'hc618;

  // Other names for the same wires on the sheet: thisstage[2:0] = in_1
endmodule

module gameover (
  input  [2:0] in_1,
  output [2:0] out_2,
  output [19:0] out_3,
  output [19:0] out_4,
  output [19:0] out_5,
  output [19:0] out_6,
  output [19:0] out_7,
  output [19:0] out_8,
  output [19:0] out_9,
  output [19:0] out_10,
  output [19:0] out_11,
  output [19:0] out_12,
  output [19:0] out_13,
  output [19:0] out_14,
  output [19:0] out_15,
  output [19:0] out_16,
  output [19:0] out_17,
  output [19:0] out_18,
  output [19:0] out_19,
  output [19:0] out_20,
  output [19:0] out_21,
  output [19:0] out_22,
  output [19:0] out_23,
  output [19:0] out_24,
  output [19:0] out_25,
  output [19:0] out_26,
  output [19:0] out_27
);


  assign out_2 = 3'b100;
  assign out_3 = {20{1'b0}};
  assign out_4 = 20'h3ba2e;
  assign out_5 = 20'h42a28;
  assign out_6 = 20'h82b68;
  assign out_7 = 20'h9ab6e;
  assign out_8 = 20'h4baa8;
  assign out_9 = 20'h6aa28;
  assign out_10 = 20'h3aa2e;
  assign out_11 = {20{1'b0}};
  assign out_12 = {20{1'b0}};
  assign out_13 = 20'hf45de;
  assign out_14 = 20'h94512;
  assign out_15 = 20'h94512;
  assign out_16 = 20'h929dc;
  assign out_17 = 20'h92912;
  assign out_18 = 20'h92912;
  assign out_19 = 20'hf11d2;
  assign out_20 = {20{1'b0}};
  assign out_21 = {20{1'b0}};
  assign out_22 = {20{1'b0}};
  assign out_23 = {20{1'b0}};
  assign out_24 = {20{1'b0}};
  assign out_25 = {20{1'b0}};
  assign out_26 = {20{1'b0}};
  assign out_27 = {20{1'b0}};

  // Other names for the same wires on the sheet: thisstage[2:0] = in_1
endmodule

module mux (
  input  in_1,
  input  [2:0] in_2,
  input  [6:0] keyboard,
  output [19:0] out_4,
  output [19:0] out_5,
  output [19:0] out_6,
  output [19:0] out_7,
  output [19:0] out_8,
  output [19:0] out_9,
  output [19:0] out_10,
  output [19:0] out_11,
  output [19:0] out_12,
  output [19:0] out_13,
  output [19:0] out_14,
  output [19:0] out_15,
  output [2:0] out_16,
  output out_17,
  output [19:0] out_18,
  output [19:0] out_19,
  output [19:0] out_20,
  output [19:0] out_21,
  output [19:0] out_22,
  output [19:0] out_23,
  output [19:0] out_24,
  output [19:0] out_25,
  output [19:0] out_26,
  output [3:0] out_27,
  output [19:0] out_28,
  output [19:0] out_29,
  output [19:0] out_30,
  output [19:0] out_31,
  output [2:0] out_32
);

  wire and_7_out, clock_1_out, clock_2_out, clock_3_out, comparator_1_eq, comparator_2_eq, comparator_3_eq,
       comparator_4_eq, comparator_5_eq, comparator_7_eq, comparator_8_eq, comparator_9_eq, comparator_10_eq,
       comparator_11_eq, comparator_12_eq, gg1, gg2, gg3, not_1_out, not_2_out, or_1_out, reset, undriven,
       undriven_2, undriven_3;
  wire [0:0] comparator_6_eq;
  wire [2:0] and_5_out, and_6_out, multiplexer_1_out, prestage, st1, st2, st3, st4, st5;
  wire [8:0] multiplexer_2_out, multiplexer_4_out, subtractor_1_out;
  wire [8:4] \end ;
  wire [19:0] _1s1, _1s2, _1s3, _1s4, _1s5, _1s6, _1s7, _1s8, _1s9, _1s10, _1s11, _1s12, _1s13, _1s14, _1s15,
       _1s16, _1s17, _1s18, _1s19, _1s20, _1s21, _1s22, _1s23, _1s24, _1s25, _2s1, _2s2, _2s3, _2s4, _2s5,
       _2s6, _2s7, _2s8, _2s9, _2s10, _2s11, _2s12, _2s13, _2s14, _2s15, _2s16, _2s17, _2s18, _2s19, _2s20,
       _2s21, _2s22, _2s23, _2s24, _2s25, _3s1, _3s2, _3s3, _3s4, _3s5, _3s6, _3s7, _3s8, _3s9, _3s10, _3s11,
       _3s12, _3s13, _3s14, _3s15, _3s16, _3s17, _3s18, _3s19, _3s20, _3s21, _3s22, _3s23, _3s24, _3s25, ov1,
       ov2, ov3, ov4, ov5, ov6, ov7, ov8, ov9, ov10, ov11, ov12, ov13, ov14, ov15, ov16, ov17, ov18, ov19,
       ov20, ov21, ov22, ov23, ov24, ov25, v1, v2, v3, v4, v5, v6, v7, v8, v9, v10, v11, v12, v13, v14, v15,
       v16, v17, v18, v19, v20, v21, v22, v23, v24, v25;

  Comparator #(.width(3)) comparator_1 (.a(out_32), .b(3'b010), .eq(comparator_1_eq));  // open: gt, lt
  stage1 stage1_1 (
    .in_1(reset), .in_2(out_32), .out_4(st1), .out_5(_1s1), .out_6(_1s2), .out_7(_1s3), .out_8(_1s4),
    .out_9(_1s5), .out_10(_1s6), .out_11(_1s7), .out_12(_1s8), .out_13(_1s9), .out_14(_1s10), .out_15(_1s11),
    .out_16(_1s12), .out_17(_1s13), .out_18(_1s14), .out_19(_1s15), .out_20(_1s16), .out_21(_1s17),
    .out_22(_1s18), .out_23(_1s19), .out_24(_1s20), .out_25(_1s21), .out_26(_1s22), .out_27(_1s23),
    .out_28(_1s24), .out_29(_1s25), .in_3(keyboard), .out_30(gg1));
  Multiplexer #(.select(3), .width(3)) multiplexer_1 (
    .in0(out_32), .in1(3'b001), .in2(3'b010), .in4(3'b011), .out(multiplexer_1_out), .sel(and_6_out));  // open: in3, in5, in6, in7, en
  and and_1 (and_6_out[2], comparator_1_eq, comparator_3_eq);
  Subtractor #(.width(9)) subtractor_1 (.a({\end , out_27}), .b(9'h1), .out(subtractor_1_out));  // open: bin, bout
  and and_2 (and_5_out[2], comparator_2_eq, gg1);
  Comparator #(.width(3)) comparator_2 (.a(out_32), .b(3'b000), .eq(comparator_2_eq));  // open: gt, lt
  Comparator #(.width(3)) comparator_3 (.a(st3), .b(3'b011), .eq(comparator_3_eq));  // open: gt, lt
  Multiplexer #(.select(3), .width(9)) multiplexer_2 (
    .in0({\end , out_27}), .in1(subtractor_1_out), .in2(subtractor_1_out), .in3({\end , out_27}),
    .in4(subtractor_1_out), .in5({\end , out_27}), .in6({\end , out_27}), .in7({\end , out_27}),
    .out(multiplexer_2_out), .sel(and_5_out));  // open: en
  and and_3 (and_5_out[1], comparator_4_eq, gg2);
  Comparator #(.width(3)) comparator_4 (.a(out_32), .b(3'b001), .eq(comparator_4_eq));  // open: gt, lt
  Multiplexer #(.select(3), .width(3)) multiplexer_3 (
    .in0(multiplexer_1_out), .in1(3'b100), .out(prestage), .sel({2'b00, comparator_6_eq[0]}));  // open: in2, in3, in4, in5, in6, in7, en
  Comparator #(.width(3)) comparator_5 (.a(out_32), .b(3'b001), .eq(comparator_5_eq));  // open: gt, lt
  stage2 stage2_1 (
    .out_4(st2), .in_2(out_32), .in_3(keyboard), .in_1(reset), .out_5(_2s1), .out_6(_2s2), .out_7(_2s3),
    .out_8(_2s4), .out_9(_2s5), .out_10(_2s6), .out_11(_2s7), .out_12(_2s8), .out_13(_2s9), .out_14(_2s10),
    .out_15(_2s11), .out_16(_2s12), .out_17(_2s13), .out_18(_2s14), .out_19(_2s15), .out_20(_2s16),
    .out_21(_2s17), .out_22(_2s18), .out_23(_2s19), .out_24(_2s20), .out_25(_2s21), .out_26(_2s22),
    .out_27(_2s23), .out_28(_2s24), .out_29(_2s25), .out_30(gg2));
  Comparator #(.width(9)) comparator_6 (.a({9{1'b0}}), .b({\end , out_27}), .eq(comparator_6_eq[0]));  // open: gt, lt
  and and_4 (and_6_out[1], comparator_5_eq, comparator_8_eq);
  Multiplexer #(.width(9)) multiplexer_4 (
    .in0(multiplexer_2_out), .in1(9'h5), .out(multiplexer_4_out), .sel(in_1));  // open: en
  and and_5 (and_5_out[0], comparator_7_eq, gg3);
  Comparator #(.width(3)) comparator_7 (.a(out_32), .b(3'b010), .eq(comparator_7_eq));  // open: gt, lt
  Comparator #(.width(3)) comparator_8 (.a(st2), .b(3'b010), .eq(comparator_8_eq));  // open: gt, lt
  Register #(.width(9)) register_1 (
    .D(multiplexer_4_out), .Q({\end , out_27}), .clk(clock_1_out), .clr(undriven));  // open: en
  Clock clock_1 (.out(clock_1_out));
  Multiplexer #(.width(3)) multiplexer_5 (.in0(prestage), .in1(in_2), .out(out_16), .sel(in_1));  // open: en
  stage3 stage3_1 (
    .in_1(reset), .out_4(st3), .in_2(out_32), .out_5(_3s1), .out_6(_3s2), .out_7(_3s3), .out_8(_3s4),
    .out_9(_3s5), .out_10(_3s6), .out_11(_3s7), .out_12(_3s8), .out_13(_3s9), .out_14(_3s10), .out_15(_3s11),
    .out_16(_3s12), .out_17(_3s13), .out_18(_3s14), .out_19(_3s15), .out_20(_3s16), .out_21(_3s17),
    .out_22(_3s18), .out_23(_3s19), .out_24(_3s20), .out_25(_3s21), .out_26(_3s22), .out_27(_3s23),
    .out_28(_3s24), .out_29(_3s25), .in_3(keyboard), .out_30(gg3));
  Register #(.width(3)) register_2 (.D(out_16), .Q(out_32), .clk(clock_2_out), .clr(undriven_2));  // open: en
  Clock clock_2 (.out(clock_2_out));
  and and_6 (and_6_out[0], comparator_9_eq, comparator_10_eq);
  Comparator #(.width(3)) comparator_9 (.a(out_32), .b(3'b000), .eq(comparator_9_eq));  // open: gt, lt
  Comparator #(.width(3)) comparator_10 (.a(st1), .b(3'b001), .eq(comparator_10_eq));  // open: gt, lt
  victory victory_1 (
    .out_3(v1), .out_4(v2), .out_5(v3), .out_6(v4), .out_7(v5), .out_8(v6), .out_9(v7), .out_10(v8),
    .out_11(v9), .out_12(v10), .out_13(v11), .out_14(v12), .out_15(v13), .out_16(v14), .out_17(v15),
    .out_18(v16), .out_19(v17), .out_20(v18), .out_21(v19), .out_22(v20), .out_23(v21), .out_24(v22),
    .out_25(v23), .out_26(v24), .out_27(v25), .in_1(out_32), .out_2(st4));
  Comparator #(.width(3)) comparator_11 (.a(out_32), .b(prestage), .eq(comparator_11_eq));  // open: gt, lt
  Multiplexer multiplexer_6 (.in0(1'b0), .in1(1'b1), .out(out_17), .sel(or_1_out));  // open: en
  or or_1 (or_1_out, in_1, and_7_out);
  and and_7 (and_7_out, not_1_out, not_2_out);
  not not_1 (not_1_out, comparator_11_eq);
  gameover gameover_1 (
    .out_2(st5), .out_3(ov1), .in_1(out_32), .out_4(ov2), .out_5(ov3), .out_6(ov4), .out_7(ov5), .out_8(ov6),
    .out_9(ov7), .out_10(ov8), .out_11(ov9), .out_12(ov10), .out_13(ov11), .out_14(ov12), .out_15(ov13),
    .out_16(ov14), .out_17(ov15), .out_18(ov16), .out_19(ov17), .out_20(ov18), .out_21(ov19), .out_22(ov20),
    .out_23(ov21), .out_24(ov22), .out_25(ov23), .out_26(ov24), .out_27(ov25));
  Register #(.width(1)) register_3 (.D(out_17), .Q(reset), .clk(clock_3_out), .clr(undriven_3));  // open: en
  Clock clock_3 (.out(clock_3_out));
  not not_2 (not_2_out, comparator_12_eq);
  Comparator #(.width(3)) comparator_12 (.a(3'b000), .b(prestage), .eq(comparator_12_eq));  // open: gt, lt
  Multiplexer #(.select(3), .width(20)) multiplexer_7 (
    .in0(_1s1), .in1(_2s1), .in2(_3s1), .in3(v1), .in4(ov1), .out(out_4), .sel(out_32));  // open: in5, in6, in7, en
  Multiplexer #(.select(3), .width(20)) multiplexer_8 (
    .in0(_1s4), .in1(_2s4), .in2(_3s4), .in3(v4), .in4(ov4), .out(out_7), .sel(out_32));  // open: in5, in6, in7, en
  Multiplexer #(.select(3), .width(20)) multiplexer_9 (
    .in0(_1s7), .in1(_2s7), .in2(_3s7), .in3(v7), .in4(ov7), .out(out_10), .sel(out_32));  // open: in5, in6, in7, en
  Multiplexer #(.select(3), .width(20)) multiplexer_10 (
    .in0(_1s10), .in1(_2s10), .in2(_3s10), .in3(v10), .in4(ov10), .out(out_13), .sel(out_32));  // open: in5, in6, in7, en
  Multiplexer #(.select(3), .width(20)) multiplexer_11 (
    .in0(_1s13), .in1(_2s13), .in2(_3s13), .in3(v13), .in4(ov13), .out(out_18), .sel(out_32));  // open: in5, in6, in7, en
  Multiplexer #(.select(3), .width(20)) multiplexer_12 (
    .in0(_1s16), .in1(_2s16), .in2(_3s16), .in3(v16), .in4(ov16), .out(out_21), .sel(out_32));  // open: in5, in6, in7, en
  Multiplexer #(.select(3), .width(20)) multiplexer_13 (
    .in0(_1s19), .in1(_2s19), .in2(_3s19), .in3(v19), .in4(ov19), .out(out_24), .sel(out_32));  // open: in5, in6, in7, en
  Multiplexer #(.select(3), .width(20)) multiplexer_14 (
    .in0(_1s22), .in1(_2s22), .in2(_3s22), .in3(v22), .in4(ov22), .out(out_28), .sel(out_32));  // open: in5, in6, in7, en
  Multiplexer #(.select(3), .width(20)) multiplexer_15 (
    .in0(_1s2), .in1(_2s2), .in2(_3s2), .in3(v2), .in4(ov2), .out(out_5), .sel(out_32));  // open: in5, in6, in7, en
  Multiplexer #(.select(3), .width(20)) multiplexer_16 (
    .in0(_1s5), .in1(_2s5), .in2(_3s5), .in3(v5), .in4(ov5), .out(out_8), .sel(out_32));  // open: in5, in6, in7, en
  Multiplexer #(.select(3), .width(20)) multiplexer_17 (
    .in0(_1s8), .in1(_2s8), .in2(_3s8), .in3(v8), .in4(ov8), .out(out_11), .sel(out_32));  // open: in5, in6, in7, en
  Multiplexer #(.select(3), .width(20)) multiplexer_18 (
    .in0(_1s11), .in1(_2s11), .in2(_3s11), .in3(v11), .in4(ov11), .out(out_14), .sel(out_32));  // open: in5, in6, in7, en
  Multiplexer #(.select(3), .width(20)) multiplexer_19 (
    .in0(_1s14), .in1(_2s14), .in2(_3s14), .in3(v14), .in4(ov14), .out(out_19), .sel(out_32));  // open: in5, in6, in7, en
  Multiplexer #(.select(3), .width(20)) multiplexer_20 (
    .in0(_1s17), .in1(_2s17), .in2(_3s17), .in3(v17), .in4(ov17), .out(out_22), .sel(out_32));  // open: in5, in6, in7, en
  Multiplexer #(.select(3), .width(20)) multiplexer_21 (
    .in0(_1s20), .in1(_2s20), .in2(_3s20), .in3(v20), .in4(ov20), .out(out_25), .sel(out_32));  // open: in5, in6, in7, en
  Multiplexer #(.select(3), .width(20)) multiplexer_22 (
    .in0(_1s23), .in1(_2s23), .in2(_3s23), .in3(v23), .in4(ov23), .out(out_29), .sel(out_32));  // open: in5, in6, in7, en
  Multiplexer #(.select(3), .width(20)) multiplexer_23 (
    .in0(_1s3), .in1(_2s3), .in2(_3s3), .in3(v3), .in4(ov3), .out(out_6), .sel(out_32));  // open: in5, in6, in7, en
  Multiplexer #(.select(3), .width(20)) multiplexer_24 (
    .in0(_1s6), .in1(_2s6), .in2(_3s6), .in3(v6), .in4(ov6), .out(out_9), .sel(out_32));  // open: in5, in6, in7, en
  Multiplexer #(.select(3), .width(20)) multiplexer_25 (
    .in0(_1s9), .in1(_2s9), .in2(_3s9), .in3(v9), .in4(ov9), .out(out_12), .sel(out_32));  // open: in5, in6, in7, en
  Multiplexer #(.select(3), .width(20)) multiplexer_26 (
    .in0(_1s12), .in1(_2s12), .in2(_3s12), .in3(v12), .in4(ov12), .out(out_15), .sel(out_32));  // open: in5, in6, in7, en
  Multiplexer #(.select(3), .width(20)) multiplexer_27 (
    .in0(_1s15), .in1(_2s15), .in2(_3s15), .in3(v15), .in4(ov15), .out(out_20), .sel(out_32));  // open: in5, in6, in7, en
  Multiplexer #(.select(3), .width(20)) multiplexer_28 (
    .in0(_1s18), .in1(_2s18), .in2(_3s18), .in3(v18), .in4(ov18), .out(out_23), .sel(out_32));  // open: in5, in6, in7, en
  Multiplexer #(.select(3), .width(20)) multiplexer_29 (
    .in0(_1s21), .in1(_2s21), .in2(_3s21), .in3(v21), .in4(ov21), .out(out_26), .sel(out_32));  // open: in5, in6, in7, en
  Multiplexer #(.select(3), .width(20)) multiplexer_30 (
    .in0(_1s24), .in1(_2s24), .in2(_3s24), .in3(v24), .in4(ov24), .out(out_30), .sel(out_32));  // open: in5, in6, in7, en
  Multiplexer #(.select(3), .width(20)) multiplexer_31 (
    .in0(_1s25), .in1(_2s25), .in2(_3s25), .in3(v25), .in4(ov25), .out(out_31), .sel(out_32));  // open: in5, in6, in7, en

  // Other names for the same wires on the sheet: end[3:0] = out_27; stage[2:0] = out_32; start = in_1;
  //   startstage[2:0] = in_2
endmodule
